// Logisim project circuit.circ as structural Verilog: 35 circuits, main circuit main
module main (
  input  memReadSignal,
  input  readPC_Signal,
  input  memWriteSignal,
  input  cmpSignal,
  input  regWriteSignal
);

  wire and_1_out, and_2_out, and_3_out, CARY_ouput, flag_Clock_out, ja_out, jae_out, jb_out, jbe_out, je_out,
       my_16bit_comparator_1_cary_flag, my_16bit_comparator_1_zero_flag, my_control_unit_1_add,
       my_control_unit_1_addi, my_control_unit_1_and, my_control_unit_1_andi, my_control_unit_1_cmp,
       my_control_unit_1_ja, my_control_unit_1_jae, my_control_unit_1_jb, my_control_unit_1_jbe,
       my_control_unit_1_je, my_control_unit_1_jump, my_control_unit_1_ld, my_control_unit_1_st, not_1_out,
       not_2_out, or_1_out, or_2_out, or_3_out, pc_Clock_out, ram_clock_out, regClock_out, ZERO_ouput;
  wire [1:0] alu_selector_1_selection;
  wire [2:0] my_control_unit_1_src1, my_control_unit_1_src1_2, my_control_unit_1_src2;
  wire [9:0] my_control_unit_1_ram_adress;
  wire [15:0] my_2_1_16bit_mux_1_output, my_2_1_16bit_mux_2_output, my_16bit_fadder_1_output,
       my_alu_1_output, my_control_unit_1_immediate, my_control_unit_1_jump_adress,
       my_program_counter_1_output, my_register_file_1_out_7, my_register_file_1_src1_data,
       my_register_file_1_src2_data, ram_1_data, rom_1_data;

  my_16bit_fadder my_16bit_fadder_1 (
    .a15_a0(my_program_counter_1_output), .b15_b0(my_control_unit_1_jump_adress), .cary_in(1'b0),
    .\output (my_16bit_fadder_1_output));  // open: cary_out
  my_16bit_comparator my_16bit_comparator_1 (
    .input1(my_register_file_1_out_7), .input2(my_register_file_1_src1_data),
    .cary_flag(my_16bit_comparator_1_cary_flag), .zero_flag(my_16bit_comparator_1_zero_flag));
  flag ZERO (.\input (my_16bit_comparator_1_zero_flag), .ouput(ZERO_ouput), .enable(and_1_out), .clk(flag_Clock_out));
  my_program_counter my_program_counter_1 (
    .if_0_add_1_else_jump(or_1_out), .enable(readPC_Signal), .\output (my_program_counter_1_output),
    .jump_adress(my_16bit_fadder_1_output), .clock(pc_Clock_out));
  and and_1 (and_1_out, cmpSignal, my_control_unit_1_cmp);
  flag CARY (.\input (my_16bit_comparator_1_cary_flag), .ouput(CARY_ouput), .enable(and_1_out), .clk(flag_Clock_out));
  not not_1 (not_1_out, ZERO_ouput);
  not not_2 (not_2_out, CARY_ouput);
  and ja (ja_out, my_control_unit_1_ja, not_1_out, not_2_out);
  and je (je_out, ZERO_ouput, not_2_out, my_control_unit_1_je);
  ROM #(.addrWidth(16), .dataWidth(16)) rom_1 (.addr(my_program_counter_1_output), .data(rom_1_data), .sel(1'b1));
  and jb (jb_out, not_1_out, my_control_unit_1_jb, CARY_ouput);
  or or_1 (or_1_out, ja_out, je_out, jb_out, jae_out, jbe_out, my_control_unit_1_jump);
  Clock pc_Clock (.out(pc_Clock_out));
  and jae (jae_out, not_2_out, my_control_unit_1_jae);
  and jbe (jbe_out, ZERO_ouput, CARY_ouput, my_control_unit_1_jbe);
  ALU_Selector alu_selector_1 (
    .\and (my_control_unit_1_and), .add(my_control_unit_1_add), .\andı (my_control_unit_1_andi),
    .\addı (my_control_unit_1_addi), .selection(alu_selector_1_selection));
  my_ALU my_alu_1 (
    .input1(my_register_file_1_src1_data), .input2(my_2_1_16bit_mux_1_output), .\output (my_alu_1_output),
    .opcode(alu_selector_1_selection));
  Clock flag_Clock (.out(flag_Clock_out));
  Clock regClock (.out(regClock_out));
  Clock ram_clock (.out(ram_clock_out));
  my_control_unit my_control_unit_1 (
    .\input (rom_1_data), .jump_adress(my_control_unit_1_jump_adress), .src2(my_control_unit_1_src2),
    .src1(my_control_unit_1_src1), .src1_2(my_control_unit_1_src1_2),
    .immediate(my_control_unit_1_immediate), .ram_adress(my_control_unit_1_ram_adress),
    .JAE(my_control_unit_1_jae), .JBE(my_control_unit_1_jbe), .JB(my_control_unit_1_jb),
    .JA(my_control_unit_1_ja), .JE(my_control_unit_1_je), .JUMP(my_control_unit_1_jump),
    .CMP(my_control_unit_1_cmp), .ADDI(my_control_unit_1_addi), .ANDI(my_control_unit_1_andi),
    .ST(my_control_unit_1_st), .LD(my_control_unit_1_ld), .ADD(my_control_unit_1_add),
    .AND(my_control_unit_1_and));
  my_2_1_16bit_mux my_2_1_16bit_mux_1 (
    .input1(my_register_file_1_src2_data), .input2(my_control_unit_1_immediate),
    .\output (my_2_1_16bit_mux_1_output), .selector(or_2_out));
  my_register_file my_register_file_1 (
    .dest_src_adr(my_control_unit_1_src1_2), .src1_data(my_register_file_1_src1_data),
    .src2_data(my_register_file_1_src2_data), .write(and_2_out), .clk(regClock_out),
    .write_data(my_2_1_16bit_mux_2_output), .src1_adr(my_control_unit_1_src1),
    .src2_adr(my_control_unit_1_src2), .out_7(my_register_file_1_out_7));
  my_2_1_16bit_mux my_2_1_16bit_mux_2 (
    .input1(my_alu_1_output), .input2(ram_1_data), .\output (my_2_1_16bit_mux_2_output),
    .selector(my_control_unit_1_ld));
  and and_2 (and_2_out, regWriteSignal, or_3_out);
  or or_2 (or_2_out, my_control_unit_1_andi, my_control_unit_1_addi);
  or or_3 (or_3_out, my_control_unit_1_and, my_control_unit_1_add, my_control_unit_1_ld, my_control_unit_1_andi, my_control_unit_1_addi);
  RAM #(.addrWidth(10), .dataWidth(16), .bus("separate")) ram_1 (
    .addr(my_control_unit_1_ram_adress), .din(my_register_file_1_out_7), .data(ram_1_data), .str(and_3_out),
    .clk(ram_clock_out), .ld(memReadSignal));  // open: sel, clr
  and and_3 (and_3_out, my_control_unit_1_st, memWriteSignal);

  // Notes on the sheet:
  //   Instruction Memory
  //   contents of rom_1 (hex, n*v repeats v):
  //   195 30b 2216 3e0c 4ac3 5f3b 196 7035 7fe4 802a 9044 a060 b017 c00e
  //   This Part is not finished yet.
  //   Signals will be associated with control unit
  //   At 3 iteration of Project
  //   Data Memory
endmodule

module my_16bit_reg (
  input  [15:0] \input ,
  input  write,
  input  clock,
  output [15:0] \output 
);

  wire my_2_1_1bit_mux_1_output, my_2_1_1bit_mux_2_output, my_2_1_1bit_mux_3_output,
       my_2_1_1bit_mux_4_output, my_2_1_1bit_mux_5_output, my_2_1_1bit_mux_6_output,
       my_2_1_1bit_mux_7_output, my_2_1_1bit_mux_8_output, my_2_1_1bit_mux_9_output,
       my_2_1_1bit_mux_10_output, my_2_1_1bit_mux_11_output, my_2_1_1bit_mux_12_output,
       my_2_1_1bit_mux_13_output, my_2_1_1bit_mux_14_output, my_2_1_1bit_mux_15_output,
       my_2_1_1bit_mux_16_output, not_1_out;

  not not_1 (not_1_out, write);
  my_2_1_1bit_mux my_2_1_1bit_mux_1 (
    .input1(\input [0]), .input2(\output [0]), .selector(not_1_out), .\output (my_2_1_1bit_mux_1_output));
  D_Flip_Flop d_ff_1 (
    .clk(clock), .D(my_2_1_1bit_mux_1_output), .Q(\output [0]), .en(write));  // open: Qn, preset, reset
  my_2_1_1bit_mux my_2_1_1bit_mux_2 (
    .input1(\input [1]), .input2(\output [1]), .selector(not_1_out), .\output (my_2_1_1bit_mux_2_output));
  my_2_1_1bit_mux my_2_1_1bit_mux_3 (
    .input1(\input [2]), .input2(\output [2]), .selector(not_1_out), .\output (my_2_1_1bit_mux_3_output));
  D_Flip_Flop d_ff_2 (
    .clk(clock), .D(my_2_1_1bit_mux_2_output), .Q(\output [1]), .en(write));  // open: Qn, preset, reset
  my_2_1_1bit_mux my_2_1_1bit_mux_4 (
    .input1(\input [3]), .input2(\output [3]), .selector(not_1_out), .\output (my_2_1_1bit_mux_4_output));
  D_Flip_Flop d_ff_3 (
    .clk(clock), .D(my_2_1_1bit_mux_3_output), .Q(\output [2]), .en(write));  // open: Qn, preset, reset
  D_Flip_Flop d_ff_4 (
    .clk(clock), .D(my_2_1_1bit_mux_4_output), .Q(\output [3]), .en(write));  // open: Qn, preset, reset
  my_2_1_1bit_mux my_2_1_1bit_mux_5 (
    .input1(\input [4]), .input2(\output [4]), .selector(not_1_out), .\output (my_2_1_1bit_mux_5_output));
  D_Flip_Flop d_ff_5 (
    .clk(clock), .D(my_2_1_1bit_mux_5_output), .Q(\output [4]), .en(write));  // open: Qn, preset, reset
  my_2_1_1bit_mux my_2_1_1bit_mux_6 (
    .input1(\input [5]), .input2(\output [5]), .selector(not_1_out), .\output (my_2_1_1bit_mux_6_output));
  my_2_1_1bit_mux my_2_1_1bit_mux_7 (
    .input1(\input [6]), .input2(\output [6]), .selector(not_1_out), .\output (my_2_1_1bit_mux_7_output));
  D_Flip_Flop d_ff_6 (
    .clk(clock), .D(my_2_1_1bit_mux_6_output), .Q(\output [5]), .en(write));  // open: Qn, preset, reset
  my_2_1_1bit_mux my_2_1_1bit_mux_8 (
    .input1(\input [7]), .input2(\output [7]), .selector(not_1_out), .\output (my_2_1_1bit_mux_8_output));
  D_Flip_Flop d_ff_7 (
    .clk(clock), .D(my_2_1_1bit_mux_7_output), .Q(\output [6]), .en(write));  // open: Qn, preset, reset
  D_Flip_Flop d_ff_8 (
    .clk(clock), .D(my_2_1_1bit_mux_8_output), .Q(\output [7]), .en(write));  // open: Qn, preset, reset
  my_2_1_1bit_mux my_2_1_1bit_mux_9 (
    .input1(\input [8]), .input2(\output [8]), .selector(not_1_out), .\output (my_2_1_1bit_mux_9_output));
  D_Flip_Flop d_ff_9 (
    .clk(clock), .D(my_2_1_1bit_mux_9_output), .Q(\output [8]), .en(write));  // open: Qn, preset, reset
  my_2_1_1bit_mux my_2_1_1bit_mux_10 (
    .input1(\input [9]), .input2(\output [9]), .selector(not_1_out), .\output (my_2_1_1bit_mux_10_output));
  my_2_1_1bit_mux my_2_1_1bit_mux_11 (
    .input1(\input [10]), .input2(\output [10]), .selector(not_1_out), .\output (my_2_1_1bit_mux_11_output));
  D_Flip_Flop d_ff_10 (
    .clk(clock), .D(my_2_1_1bit_mux_10_output), .Q(\output [9]), .en(write));  // open: Qn, preset, reset
  my_2_1_1bit_mux my_2_1_1bit_mux_12 (
    .input1(\input [11]), .input2(\output [11]), .selector(not_1_out), .\output (my_2_1_1bit_mux_12_output));
  D_Flip_Flop d_ff_11 (
    .clk(clock), .D(my_2_1_1bit_mux_11_output), .Q(\output [10]), .en(write));  // open: Qn, preset, reset
  D_Flip_Flop d_ff_12 (
    .clk(clock), .D(my_2_1_1bit_mux_12_output), .Q(\output [11]), .en(write));  // open: Qn, preset, reset
  my_2_1_1bit_mux my_2_1_1bit_mux_13 (
    .input1(\input [12]), .input2(\output [12]), .selector(not_1_out), .\output (my_2_1_1bit_mux_13_output));
  D_Flip_Flop d_ff_13 (
    .clk(clock), .D(my_2_1_1bit_mux_13_output), .Q(\output [12]), .en(write));  // open: Qn, preset, reset
  my_2_1_1bit_mux my_2_1_1bit_mux_14 (
    .input1(\input [13]), .input2(\output [13]), .selector(not_1_out), .\output (my_2_1_1bit_mux_14_output));
  my_2_1_1bit_mux my_2_1_1bit_mux_15 (
    .input1(\input [14]), .input2(\output [14]), .selector(not_1_out), .\output (my_2_1_1bit_mux_15_output));
  D_Flip_Flop d_ff_14 (
    .clk(clock), .D(my_2_1_1bit_mux_14_output), .Q(\output [13]), .en(write));  // open: Qn, preset, reset
  my_2_1_1bit_mux my_2_1_1bit_mux_16 (
    .input1(\input [15]), .input2(\output [15]), .selector(not_1_out), .\output (my_2_1_1bit_mux_16_output));
  D_Flip_Flop d_ff_15 (
    .clk(clock), .D(my_2_1_1bit_mux_15_output), .Q(\output [14]), .en(write));  // open: Qn, preset, reset
  D_Flip_Flop d_ff_16 (
    .clk(clock), .D(my_2_1_1bit_mux_16_output), .Q(\output [15]), .en(write));  // open: Qn, preset, reset
endmodule

module my_3_8_decoder (
  input  in_1,
  input  in_2,
  input  in_3,
  input  load,
  output out_5,
  output out_6,
  output out_7,
  output out_8,
  output out_9,
  output out_10,
  output out_11,
  output out_12
);

  wire not_1_out, not_2_out, not_3_out, not_4_out, not_5_out, not_6_out, not_7_out, not_8_out, not_9_out,
       not_10_out, not_11_out, not_12_out;

  not not_1 (not_1_out, in_1);
  not not_2 (not_2_out, in_2);
  not not_3 (not_3_out, in_3);
  not not_4 (not_4_out, in_1);
  not not_5 (not_5_out, in_2);
  not not_6 (not_6_out, in_1);
  not not_7 (not_7_out, in_3);
  not not_8 (not_8_out, in_1);
  not not_9 (not_9_out, in_2);
  not not_10 (not_10_out, in_3);
  not not_11 (not_11_out, in_2);
  not not_12 (not_12_out, in_3);
  and and_1 (out_5, not_1_out, not_2_out, load, not_3_out);
  and and_2 (out_6, not_4_out, not_5_out, load, in_3);
  and and_3 (out_7, not_6_out, in_2, load, not_7_out);
  and and_4 (out_8, not_8_out, in_2, load, in_3);
  and and_5 (out_9, in_1, not_9_out, load, not_10_out);
  and and_6 (out_10, in_1, not_11_out, load, in_3);
  and and_7 (out_11, in_1, in_2, load, not_12_out);
  and and_8 (out_12, in_1, in_2, load, in_3);
endmodule

module my_2_1_1bit_mux (
  input  input1,
  input  input2,
  input  selector,
  output \output 
);

  wire and_1_out, and_2_out, not_1_out;

  not not_1 (not_1_out, selector);
  and and_1 (and_1_out, input1, not_1_out);
  and and_2 (and_2_out, input2, selector);
  or or_1 (\output , and_1_out, and_2_out);
endmodule

module my_register_file (
  input  [15:0] write_data,
  input  [2:0] dest_src_adr,
  input  [2:0] src1_adr,
  input  [2:0] src2_adr,
  input  clk,
  input  write,
  output [15:0] out_7,
  output [15:0] src1_data,
  output [15:0] src2_data
);

  wire my_3_8_decoder_1_out_5, my_3_8_decoder_1_out_6, my_3_8_decoder_1_out_7, my_3_8_decoder_1_out_8,
       my_3_8_decoder_1_out_9, my_3_8_decoder_1_out_10, my_3_8_decoder_1_out_11, my_3_8_decoder_1_out_12;
  wire [15:0] my_16bit_reg_1_output, my_16bit_reg_2_output, my_16bit_reg_3_output, my_16bit_reg_4_output,
       R0_2_output, R0_3_output, R0_output, R3_output;

  my_3_8_decoder my_3_8_decoder_1 (
    .in_1(dest_src_adr[2]), .in_2(dest_src_adr[1]), .in_3(dest_src_adr[0]), .load(write),
    .out_5(my_3_8_decoder_1_out_5), .out_6(my_3_8_decoder_1_out_6), .out_7(my_3_8_decoder_1_out_7),
    .out_8(my_3_8_decoder_1_out_8), .out_9(my_3_8_decoder_1_out_9), .out_10(my_3_8_decoder_1_out_10),
    .out_11(my_3_8_decoder_1_out_11), .out_12(my_3_8_decoder_1_out_12));
  my_16bit_reg R0 (.write(my_3_8_decoder_1_out_5), .clock(clk), .\input (write_data), .\output (R0_output));
  my_16bit_reg R0_2 (.write(my_3_8_decoder_1_out_6), .clock(clk), .\input (write_data), .\output (R0_2_output));
  my_16bit_reg R0_3 (.write(my_3_8_decoder_1_out_7), .clock(clk), .\input (write_data), .\output (R0_3_output));
  my_16bit_reg R3 (.write(my_3_8_decoder_1_out_8), .clock(clk), .\input (write_data), .\output (R3_output));
  my_16bit_reg my_16bit_reg_1 (
    .write(my_3_8_decoder_1_out_9), .clock(clk), .\input (write_data), .\output (my_16bit_reg_1_output));
  my_16bit_reg my_16bit_reg_2 (
    .write(my_3_8_decoder_1_out_10), .clock(clk), .\input (write_data), .\output (my_16bit_reg_2_output));
  my_16bit_reg my_16bit_reg_3 (
    .write(my_3_8_decoder_1_out_11), .clock(clk), .\input (write_data), .\output (my_16bit_reg_3_output));
  my_16bit_reg my_16bit_reg_4 (
    .write(my_3_8_decoder_1_out_12), .clock(clk), .\input (write_data), .\output (my_16bit_reg_4_output));
  my_8_1_16bit_mux my_8_1_16bit_mux_1 (
    .in_1(R0_output), .in_2(R0_2_output), .in_3(R0_3_output), .in_4(R3_output), .in_5(my_16bit_reg_1_output),
    .in_6(my_16bit_reg_2_output), .in_7(my_16bit_reg_3_output), .in_8(my_16bit_reg_4_output),
    .in_9(dest_src_adr[2]), .in_10(dest_src_adr[1]), .in_11(dest_src_adr[0]), .out_12(out_7));
  my_8_1_16bit_mux my_8_1_16bit_mux_2 (
    .in_1(R0_output), .in_2(R0_2_output), .in_3(R0_3_output), .in_4(R3_output), .in_5(my_16bit_reg_1_output),
    .in_6(my_16bit_reg_2_output), .in_7(my_16bit_reg_3_output), .in_8(my_16bit_reg_4_output),
    .in_9(src1_adr[2]), .in_10(src1_adr[1]), .in_11(src1_adr[0]), .out_12(src1_data));
  my_8_1_16bit_mux my_8_1_16bit_mux_3 (
    .in_1(R0_output), .in_2(R0_2_output), .in_3(R0_3_output), .in_4(R3_output), .in_5(my_16bit_reg_1_output),
    .in_6(my_16bit_reg_2_output), .in_7(my_16bit_reg_3_output), .in_8(my_16bit_reg_4_output),
    .in_9(src2_adr[2]), .in_10(src2_adr[1]), .in_11(src2_adr[0]), .out_12(src2_data));
endmodule

module my_2_4_decoder (
  input  in_1,
  input  in_2,
  input  in_3,
  output out_4,
  output out_5,
  output out_6,
  output out_7
);

  wire not_1_out, not_2_out, not_3_out, not_4_out;

  not not_1 (not_1_out, in_1);
  not not_2 (not_2_out, in_2);
  not not_3 (not_3_out, in_1);
  not not_4 (not_4_out, in_2);
  and and_1 (out_4, not_1_out, not_2_out, in_3);
  and and_2 (out_5, not_3_out, in_2, in_3);
  and and_3 (out_6, in_1, not_4_out, in_3);
  and and_4 (out_7, in_1, in_2, in_3);
endmodule

module my_8_1_16bit_mux (
  input  [15:0] in_1,
  input  [15:0] in_2,
  input  [15:0] in_3,
  input  [15:0] in_4,
  input  [15:0] in_5,
  input  [15:0] in_6,
  input  [15:0] in_7,
  input  [15:0] in_8,
  input  in_9,
  input  in_10,
  input  in_11,
  output [15:0] out_12
);

  wire [15:0] and_1_out, and_2_out, and_3_out, and_4_out, and_5_out, and_6_out, and_7_out, and_8_out,
       my_1_16_extender_1_output, my_1_16_extender_2_output, my_1_16_extender_3_output, not_1_out, not_2_out,
       not_3_out, not_4_out, not_5_out, not_6_out, not_7_out, not_8_out, not_9_out, not_10_out, not_11_out,
       not_12_out;

  my_1_16_extender my_1_16_extender_1 (.\input (in_9), .\output (my_1_16_extender_1_output));
  my_1_16_extender my_1_16_extender_2 (.\input (in_10), .\output (my_1_16_extender_2_output));
  assign not_1_out = ~my_1_16_extender_1_output;  // NOT_Gate not_1, 16 bits wide
  assign not_2_out = ~my_1_16_extender_2_output;  // NOT_Gate not_2, 16 bits wide
  assign not_3_out = ~my_1_16_extender_3_output;  // NOT_Gate not_3, 16 bits wide
  assign not_4_out = ~my_1_16_extender_1_output;  // NOT_Gate not_4, 16 bits wide
  assign not_5_out = ~my_1_16_extender_2_output;  // NOT_Gate not_5, 16 bits wide
  assign not_6_out = ~my_1_16_extender_1_output;  // NOT_Gate not_6, 16 bits wide
  assign not_7_out = ~my_1_16_extender_3_output;  // NOT_Gate not_7, 16 bits wide
  assign not_8_out = ~my_1_16_extender_1_output;  // NOT_Gate not_8, 16 bits wide
  assign not_9_out = ~my_1_16_extender_2_output;  // NOT_Gate not_9, 16 bits wide
  assign not_10_out = ~my_1_16_extender_3_output;  // NOT_Gate not_10, 16 bits wide
  assign not_11_out = ~my_1_16_extender_2_output;  // NOT_Gate not_11, 16 bits wide
  assign not_12_out = ~my_1_16_extender_3_output;  // NOT_Gate not_12, 16 bits wide
  my_1_16_extender my_1_16_extender_3 (.\input (in_11), .\output (my_1_16_extender_3_output));
  assign and_1_out = in_1 & not_1_out & not_2_out & not_3_out;  // AND_Gate and_1, 16 bits wide
  assign and_2_out = in_2 & not_4_out & not_5_out & my_1_16_extender_3_output;  // AND_Gate and_2, 16 bits wide
  assign and_3_out = in_3 & not_6_out & my_1_16_extender_2_output & not_7_out;  // AND_Gate and_3, 16 bits wide
  assign and_4_out = in_4 & not_8_out & my_1_16_extender_2_output & my_1_16_extender_3_output;  // AND_Gate and_4, 16 bits wide
  assign and_5_out = in_5 & my_1_16_extender_1_output & not_9_out & not_10_out;  // AND_Gate and_5, 16 bits wide
  assign and_6_out = in_6 & my_1_16_extender_1_output & not_11_out & my_1_16_extender_3_output;  // AND_Gate and_6, 16 bits wide
  assign and_7_out = in_7 & my_1_16_extender_1_output & my_1_16_extender_2_output & not_12_out;  // AND_Gate and_7, 16 bits wide
  assign and_8_out = in_8 & my_1_16_extender_1_output & my_1_16_extender_2_output & my_1_16_extender_3_output;  // AND_Gate and_8, 16 bits wide
  assign out_12 = and_1_out | and_2_out | and_3_out | and_4_out | and_5_out | and_6_out | and_7_out | and_8_out;  // OR_Gate or_1, 16 bits wide
endmodule

module my_1_3_extender (
  input  in_1,
  output [2:0] out_2
);


  assign out_2 = {3{in_1}};
endmodule

module my_ALU (
  input  [15:0] input1,
  input  [15:0] input2,
  input  [1:0] opcode,
  output [15:0] \output 
);

  wire [15:0] and_1_out, my_16bit_fadder_1_output, or_1_out;

  assign and_1_out = input1 & input2;  // AND_Gate and_1, 16 bits wide
  my_16bit_fadder my_16bit_fadder_1 (
    .a15_a0(input2), .b15_b0(input1), .cary_in(1'b0), .\output (my_16bit_fadder_1_output));  // open: cary_out
  assign or_1_out = input1 | input2;  // OR_Gate or_1, 16 bits wide
  my_4_1_16bit_mux my_mux (
    ._0(and_1_out), ._1(my_16bit_fadder_1_output), ._2(or_1_out), .in_5(opcode), .out_6(\output ));  // open: _3
endmodule

module my_1_16_extender (
  input  \input ,
  output [15:0] \output 
);


  assign \output  = {16{\input }};
endmodule

module my_4_1_16bit_mux (
  input  [15:0] _0,
  input  [15:0] _1,
  input  [15:0] _2,
  input  [15:0] _3,
  input  [1:0] in_5,
  output [15:0] out_6
);

  wire [15:0] and_1_out, and_2_out, and_3_out, and_4_out, my_1_16_extender_1_output,
       my_1_16_extender_2_output, not_1_out, not_2_out, not_3_out, not_4_out;

  my_1_16_extender my_1_16_extender_1 (.\input (in_5[1]), .\output (my_1_16_extender_1_output));
  my_1_16_extender my_1_16_extender_2 (.\input (in_5[0]), .\output (my_1_16_extender_2_output));
  assign not_1_out = ~my_1_16_extender_1_output;  // NOT_Gate not_1, 16 bits wide
  assign not_2_out = ~my_1_16_extender_2_output;  // NOT_Gate not_2, 16 bits wide
  assign not_3_out = ~my_1_16_extender_1_output;  // NOT_Gate not_3, 16 bits wide
  assign not_4_out = ~my_1_16_extender_2_output;  // NOT_Gate not_4, 16 bits wide
  assign and_1_out = _0 & not_1_out & not_2_out;  // AND_Gate and_1, 16 bits wide
  assign and_2_out = _1 & not_3_out & my_1_16_extender_2_output;  // AND_Gate and_2, 16 bits wide
  assign and_3_out = _2 & my_1_16_extender_1_output & not_4_out;  // AND_Gate and_3, 16 bits wide
  assign and_4_out = _3 & my_1_16_extender_1_output & my_1_16_extender_2_output;  // AND_Gate and_4, 16 bits wide
  assign out_6 = and_1_out | and_2_out | and_3_out | and_4_out;  // OR_Gate or_1, 16 bits wide
endmodule

module my_4_16_16bit_decoder (
  input  enable,
  input  [3:0] _4_0,
  output \and ,
  output add,
  output ld,
  output st,
  output \andı ,
  output \addı ,
  output cmp,
  output jump,
  output je,
  output ja,
  output jb,
  output jbe,
  output jae,
  output \null ,
  output null_2,
  output null_3
);

  wire not_1_out, not_2_out, not_3_out, not_4_out, not_5_out, not_6_out, not_7_out, not_8_out, not_9_out,
       not_10_out, not_11_out, not_12_out, not_13_out, not_14_out, not_15_out, not_16_out, not_17_out,
       not_18_out, not_19_out, not_20_out, not_21_out, not_22_out, not_23_out, not_24_out, not_25_out,
       not_26_out, not_27_out, not_28_out, not_29_out, not_30_out, not_31_out, not_32_out;

  not not_1 (not_1_out, _4_0[3]);
  not not_2 (not_2_out, _4_0[2]);
  and and_1 (\and , not_1_out, not_2_out, not_5_out, not_3_out, enable);
  not not_3 (not_3_out, _4_0[0]);
  not not_4 (not_4_out, _4_0[3]);
  not not_5 (not_5_out, _4_0[1]);
  not not_6 (not_6_out, _4_0[2]);
  and and_2 (add, not_4_out, not_6_out, not_8_out, _4_0[0], enable);
  not not_7 (not_7_out, _4_0[3]);
  not not_8 (not_8_out, _4_0[1]);
  not not_9 (not_9_out, _4_0[2]);
  and and_3 (ld, not_7_out, not_9_out, _4_0[1], not_12_out, enable);
  not not_10 (not_10_out, _4_0[3]);
  not not_11 (not_11_out, _4_0[2]);
  not not_12 (not_12_out, _4_0[0]);
  and and_4 (\andı , not_13_out, _4_0[2], not_14_out, not_15_out, enable);
  and and_5 (st, not_10_out, not_11_out, _4_0[1], _4_0[0], enable);
  not not_13 (not_13_out, _4_0[3]);
  not not_14 (not_14_out, _4_0[1]);
  and and_6 (\addı , not_16_out, _4_0[2], not_17_out, _4_0[0], enable);
  not not_15 (not_15_out, _4_0[0]);
  not not_16 (not_16_out, _4_0[3]);
  not not_17 (not_17_out, _4_0[1]);
  and and_7 (cmp, not_18_out, _4_0[2], _4_0[1], not_19_out, enable);
  not not_18 (not_18_out, _4_0[3]);
  and and_8 (jump, not_20_out, _4_0[2], _4_0[1], _4_0[0], enable);
  not not_19 (not_19_out, _4_0[0]);
  not not_20 (not_20_out, _4_0[3]);
  and and_9 (je, _4_0[3], not_21_out, not_22_out, not_23_out, enable);
  not not_21 (not_21_out, _4_0[2]);
  not not_22 (not_22_out, _4_0[1]);
  not not_23 (not_23_out, _4_0[0]);
  and and_10 (ja, _4_0[3], not_25_out, not_24_out, _4_0[0], enable);
  not not_24 (not_24_out, _4_0[1]);
  not not_25 (not_25_out, _4_0[2]);
  and and_11 (jb, _4_0[3], not_26_out, _4_0[1], not_27_out, enable);
  not not_26 (not_26_out, _4_0[2]);
  not not_27 (not_27_out, _4_0[0]);
  and and_12 (jbe, _4_0[3], not_28_out, _4_0[1], _4_0[0], enable);
  not not_28 (not_28_out, _4_0[2]);
  and and_13 (jae, _4_0[3], _4_0[2], not_29_out, not_30_out, enable);
  not not_29 (not_29_out, _4_0[1]);
  not not_30 (not_30_out, _4_0[0]);
  and and_14 (\null , _4_0[3], _4_0[2], not_31_out, _4_0[0], enable);
  not not_31 (not_31_out, _4_0[1]);
  and and_15 (null_2, _4_0[3], _4_0[2], _4_0[1], not_32_out, enable);
  not not_32 (not_32_out, _4_0[0]);
  and and_16 (null_3, _4_0[3], _4_0[2], _4_0[1], _4_0[0], enable);
endmodule

module my_1bit_fadder (
  input  cary_in,
  input  b,
  input  a,
  output cary_out,
  output s
);

  wire and_1_out, and_2_out, and_3_out;

  and and_1 (and_1_out, a, b);
  and and_2 (and_2_out, a, cary_in);
  or or_1 (cary_out, and_1_out, and_2_out, and_3_out);
  and and_3 (and_3_out, b, cary_in);
  ExactlyOne xor_1 (.out(s), .in0(a), .in1(b), .in2(cary_in));
endmodule

module my_2bit_full_adder (
  input  [1:0] a1a0,
  input  [1:0] b1b0,
  input  cary_in,
  output out_4,
  output [1:0] s1s0
);

  wire my_1bit_fadder_2_cary_out;

  my_1bit_fadder my_1bit_fadder_1 (
    .a(a1a0[1]), .b(b1b0[1]), .cary_in(my_1bit_fadder_2_cary_out), .cary_out(out_4), .s(s1s0[1]));
  my_1bit_fadder my_1bit_fadder_2 (
    .a(a1a0[0]), .b(b1b0[0]), .cary_in(cary_in), .cary_out(my_1bit_fadder_2_cary_out), .s(s1s0[0]));
endmodule

module my_4bit_adder (
  input  [3:0] a3a2a1a0,
  input  [3:0] b3b2b1b0,
  input  cary_in,
  output cary_out,
  output [3:0] s3s2s1s0
);

  wire my_2bit_full_adder_1_out_4;

  my_2bit_full_adder my_2bit_full_adder_1 (
    .a1a0(a3a2a1a0[1:0]), .b1b0(b3b2b1b0[1:0]), .cary_in(cary_in), .out_4(my_2bit_full_adder_1_out_4),
    .s1s0(s3s2s1s0[1:0]));
  my_2bit_full_adder my_2bit_full_adder_2 (
    .a1a0(a3a2a1a0[3:2]), .b1b0(b3b2b1b0[3:2]), .cary_in(my_2bit_full_adder_1_out_4), .out_4(cary_out),
    .s1s0(s3s2s1s0[3:2]));
endmodule

module my_8bit_fadder (
  input  cary_in,
  input  [7:0] a7a6a5a4a3a2a1,
  input  [7:0] b7b6b5b4b3b2b1,
  output cary_out,
  output [7:0] s7s6s5s4s3s2s1s0
);

  wire my_4bit_adder_2_cary_out;

  my_4bit_adder my_4bit_adder_1 (
    .a3a2a1a0(a7a6a5a4a3a2a1[7:4]), .b3b2b1b0(b7b6b5b4b3b2b1[7:4]), .cary_in(my_4bit_adder_2_cary_out),
    .cary_out(cary_out), .s3s2s1s0(s7s6s5s4s3s2s1s0[7:4]));
  my_4bit_adder my_4bit_adder_2 (
    .a3a2a1a0(a7a6a5a4a3a2a1[3:0]), .b3b2b1b0(b7b6b5b4b3b2b1[3:0]), .cary_in(cary_in),
    .cary_out(my_4bit_adder_2_cary_out), .s3s2s1s0(s7s6s5s4s3s2s1s0[3:0]));
endmodule

module my_16bit_fadder (
  input  [15:0] a15_a0,
  input  [15:0] b15_b0,
  input  cary_in,
  output cary_out,
  output [15:0] \output 
);

  wire my_8bit_fadder_2_cary_out;

  my_8bit_fadder my_8bit_fadder_1 (
    .a7a6a5a4a3a2a1(a15_a0[15:8]), .b7b6b5b4b3b2b1(b15_b0[15:8]), .cary_in(my_8bit_fadder_2_cary_out),
    .cary_out(cary_out), .s7s6s5s4s3s2s1s0(\output [15:8]));
  my_8bit_fadder my_8bit_fadder_2 (
    .a7a6a5a4a3a2a1(a15_a0[7:0]), .b7b6b5b4b3b2b1(b15_b0[7:0]), .cary_in(cary_in),
    .cary_out(my_8bit_fadder_2_cary_out), .s7s6s5s4s3s2s1s0(\output [7:0]));
endmodule

module my_6_to16_extender (
  input  [5:0] \input ,
  output [15:0] \output 
);


  assign \output  = {{11{\input [5]}}, \input [4:0]};
endmodule

module my_2_1_16bit_mux (
  input  [15:0] input1,
  input  [15:0] input2,
  input  selector,
  output [15:0] \output 
);

  wire [15:0] and_1_out, and_2_out, my_1_16_extender_1_output, not_1_out;

  assign not_1_out = ~my_1_16_extender_1_output;  // NOT_Gate not_1, 16 bits wide
  my_1_16_extender my_1_16_extender_1 (.\input (selector), .\output (my_1_16_extender_1_output));
  assign and_1_out = input1 & not_1_out;  // AND_Gate and_1, 16 bits wide
  assign and_2_out = input2 & my_1_16_extender_1_output;  // AND_Gate and_2, 16 bits wide
  assign \output  = and_1_out | and_2_out;  // OR_Gate or_1, 16 bits wide
endmodule

module my_9_to16bit_extender (
  input  [8:0] \input ,
  output [15:0] \output 
);


  assign \output  = {{7{1'b0}}, \input };
endmodule

module my_9_to_10_extender (
  input  [8:0] \input ,
  output [9:0] \output 
);


  assign \output  = {1'b0, \input };
endmodule

module my_2_1_10bit_mux (
  input  [9:0] input1,
  input  [9:0] input2,
  input  selector,
  output [9:0] \output 
);

  wire [9:0] and_1_out, and_2_out, my_1_to_10_extender_1_output, not_1_out;

  assign not_1_out = ~my_1_to_10_extender_1_output;  // NOT_Gate not_1, 10 bits wide
  my_1_to_10_extender my_1_to_10_extender_1 (.\input (selector), .\output (my_1_to_10_extender_1_output));
  assign and_1_out = input1 & not_1_out;  // AND_Gate and_1, 10 bits wide
  assign and_2_out = input2 & my_1_to_10_extender_1_output;  // AND_Gate and_2, 10 bits wide
  assign \output  = and_1_out | and_2_out;  // OR_Gate or_1, 10 bits wide
endmodule

module my_1_to_10_extender (
  input  \input ,
  output [9:0] \output 
);


  assign \output  = {10{\input }};
endmodule

module my_16bit_eq_comparator (
  input  [15:0] input2,
  input  [15:0] input1,
  output \output 
);

  wire xnor_1_out, xnor_2_out, xnor_3_out, xnor_4_out, xnor_5_out, xnor_6_out, xnor_7_out, xnor_8_out,
       xnor_9_out, xnor_10_out, xnor_11_out, xnor_12_out, xnor_13_out, xnor_14_out, xnor_15_out, xnor_16_out;

  xnor xnor_1 (xnor_1_out, input1[15], input2[15]);
  xnor xnor_2 (xnor_2_out, input1[14], input2[14]);
  xnor xnor_3 (xnor_3_out, input1[13], input2[13]);
  xnor xnor_4 (xnor_4_out, input1[12], input2[12]);
  xnor xnor_5 (xnor_5_out, input1[11], input2[11]);
  xnor xnor_6 (xnor_6_out, input1[10], input2[10]);
  xnor xnor_7 (xnor_7_out, input1[8], input2[8]);
  xnor xnor_8 (xnor_8_out, input1[9], input2[9]);
  xnor xnor_9 (xnor_9_out, input1[7], input2[7]);
  and and_1 (\output , xnor_1_out, xnor_2_out, xnor_3_out, xnor_4_out, xnor_5_out, xnor_6_out, xnor_8_out, xnor_7_out, xnor_9_out, xnor_10_out, xnor_11_out, xnor_12_out, xnor_13_out, xnor_15_out, xnor_14_out, xnor_16_out);
  xnor xnor_10 (xnor_10_out, input1[6], input2[6]);
  xnor xnor_11 (xnor_11_out, input1[5], input2[5]);
  xnor xnor_12 (xnor_12_out, input1[4], input2[4]);
  xnor xnor_13 (xnor_13_out, input1[3], input2[3]);
  xnor xnor_14 (xnor_14_out, input1[1], input2[1]);
  xnor xnor_15 (xnor_15_out, input1[2], input2[2]);
  xnor xnor_16 (xnor_16_out, input1[0], input2[0]);
endmodule

module my_1bit_comparator (
  input  input1,
  input  input2,
  output \output 
);

  wire xnor_1_out, xnor_2_out;

  xnor xnor_1 (xnor_1_out, input1, input2);
  and and_1 (\output , xnor_1_out, xnor_2_out);
  xnor xnor_2 (xnor_2_out, input1, input2);
endmodule

module my_1bit_mag_comp (
  input  input1,
  input  input2,
  input  in_gt,
  input  in_eq,
  input  in_ls,
  output out_gt,
  output out_eq,
  output out_ls
);

  wire and_1_out, and_2_out, my_1bit_comparator_1_output, not_1_out, not_2_out, not_3_out, or_3_out;

  and and_1 (and_1_out, input1, in_eq, not_1_out);
  or or_1 (out_gt, in_gt, and_1_out);
  not not_1 (not_1_out, input2);
  my_1bit_comparator my_1bit_comparator_1 (.input1(input1), .input2(input2), .\output (my_1bit_comparator_1_output));
  not not_2 (not_2_out, input1);
  and and_2 (and_2_out, not_2_out, in_eq, input2);
  or or_2 (out_ls, in_ls, and_2_out);
  or or_3 (or_3_out, out_gt, out_ls);
  not not_3 (not_3_out, or_3_out);
  and and_3 (out_eq, my_1bit_comparator_1_output, not_3_out);
endmodule

module my_1bit_less_detector (
  input  input1,
  input  input2,
  input  in_3,
  output \output 
);

  wire and_1_out, not_1_out;

  not not_1 (not_1_out, input1);
  and and_1 (and_1_out, not_1_out, input2);
  or or_1 (\output , in_3, and_1_out);
endmodule

module my_16bit_mag_comparator (
  input  [15:0] input2,
  input  [15:0] input1,
  output gt,
  output eq,
  output ls
);

  wire my_1bit_mag_comp_1_out_eq, my_1bit_mag_comp_1_out_gt, my_1bit_mag_comp_1_out_ls,
       my_1bit_mag_comp_2_out_eq, my_1bit_mag_comp_2_out_gt, my_1bit_mag_comp_2_out_ls,
       my_1bit_mag_comp_3_out_eq, my_1bit_mag_comp_3_out_gt, my_1bit_mag_comp_3_out_ls,
       my_1bit_mag_comp_4_out_eq, my_1bit_mag_comp_4_out_gt, my_1bit_mag_comp_4_out_ls,
       my_1bit_mag_comp_5_out_eq, my_1bit_mag_comp_5_out_gt, my_1bit_mag_comp_5_out_ls,
       my_1bit_mag_comp_6_out_eq, my_1bit_mag_comp_6_out_gt, my_1bit_mag_comp_6_out_ls,
       my_1bit_mag_comp_7_out_eq, my_1bit_mag_comp_7_out_gt, my_1bit_mag_comp_7_out_ls,
       my_1bit_mag_comp_8_out_eq, my_1bit_mag_comp_8_out_gt, my_1bit_mag_comp_8_out_ls,
       my_1bit_mag_comp_9_out_eq, my_1bit_mag_comp_9_out_gt, my_1bit_mag_comp_9_out_ls,
       my_1bit_mag_comp_10_out_eq, my_1bit_mag_comp_10_out_gt, my_1bit_mag_comp_10_out_ls,
       my_1bit_mag_comp_11_out_eq, my_1bit_mag_comp_11_out_gt, my_1bit_mag_comp_11_out_ls,
       my_1bit_mag_comp_12_out_eq, my_1bit_mag_comp_12_out_gt, my_1bit_mag_comp_12_out_ls,
       my_1bit_mag_comp_13_out_eq, my_1bit_mag_comp_13_out_gt, my_1bit_mag_comp_13_out_ls,
       my_1bit_mag_comp_14_out_eq, my_1bit_mag_comp_14_out_gt, my_1bit_mag_comp_14_out_ls,
       my_1bit_mag_comp_15_out_eq, my_1bit_mag_comp_15_out_gt, my_1bit_mag_comp_15_out_ls;

  my_1bit_mag_comp my_1bit_mag_comp_1 (
    .in_gt(1'b0), .in_eq(1'b1), .in_ls(1'b0), .input1(input1[15]), .input2(input1[15]),
    .out_gt(my_1bit_mag_comp_1_out_gt), .out_eq(my_1bit_mag_comp_1_out_eq), .out_ls(my_1bit_mag_comp_1_out_ls));
  my_1bit_mag_comp my_1bit_mag_comp_2 (
    .in_gt(my_1bit_mag_comp_1_out_gt), .in_eq(my_1bit_mag_comp_1_out_eq), .in_ls(my_1bit_mag_comp_1_out_ls),
    .input1(input1[14]), .input2(input2[14]), .out_gt(my_1bit_mag_comp_2_out_gt),
    .out_eq(my_1bit_mag_comp_2_out_eq), .out_ls(my_1bit_mag_comp_2_out_ls));
  my_1bit_mag_comp my_1bit_mag_comp_3 (
    .in_gt(my_1bit_mag_comp_2_out_gt), .in_eq(my_1bit_mag_comp_2_out_eq), .in_ls(my_1bit_mag_comp_2_out_ls),
    .input1(input1[13]), .input2(input2[13]), .out_gt(my_1bit_mag_comp_3_out_gt),
    .out_eq(my_1bit_mag_comp_3_out_eq), .out_ls(my_1bit_mag_comp_3_out_ls));
  my_1bit_mag_comp my_1bit_mag_comp_4 (
    .in_gt(my_1bit_mag_comp_3_out_gt), .in_eq(my_1bit_mag_comp_3_out_eq), .in_ls(my_1bit_mag_comp_3_out_ls),
    .input1(input1[12]), .input2(input2[12]), .out_gt(my_1bit_mag_comp_4_out_gt),
    .out_eq(my_1bit_mag_comp_4_out_eq), .out_ls(my_1bit_mag_comp_4_out_ls));
  my_1bit_mag_comp my_1bit_mag_comp_5 (
    .in_gt(my_1bit_mag_comp_4_out_gt), .in_eq(my_1bit_mag_comp_4_out_eq), .in_ls(my_1bit_mag_comp_4_out_ls),
    .input1(input1[11]), .input2(input2[11]), .out_gt(my_1bit_mag_comp_5_out_gt),
    .out_eq(my_1bit_mag_comp_5_out_eq), .out_ls(my_1bit_mag_comp_5_out_ls));
  my_1bit_mag_comp my_1bit_mag_comp_6 (
    .in_gt(my_1bit_mag_comp_5_out_gt), .in_eq(my_1bit_mag_comp_5_out_eq), .in_ls(my_1bit_mag_comp_5_out_ls),
    .input1(input1[10]), .input2(input2[10]), .out_gt(my_1bit_mag_comp_6_out_gt),
    .out_eq(my_1bit_mag_comp_6_out_eq), .out_ls(my_1bit_mag_comp_6_out_ls));
  my_1bit_mag_comp my_1bit_mag_comp_7 (
    .in_gt(my_1bit_mag_comp_6_out_gt), .in_eq(my_1bit_mag_comp_6_out_eq), .in_ls(my_1bit_mag_comp_6_out_ls),
    .input1(input1[9]), .input2(input2[9]), .out_gt(my_1bit_mag_comp_7_out_gt),
    .out_eq(my_1bit_mag_comp_7_out_eq), .out_ls(my_1bit_mag_comp_7_out_ls));
  my_1bit_mag_comp my_1bit_mag_comp_8 (
    .in_gt(my_1bit_mag_comp_7_out_gt), .in_eq(my_1bit_mag_comp_7_out_eq), .in_ls(my_1bit_mag_comp_7_out_ls),
    .input1(input1[8]), .input2(input2[8]), .out_gt(my_1bit_mag_comp_8_out_gt),
    .out_eq(my_1bit_mag_comp_8_out_eq), .out_ls(my_1bit_mag_comp_8_out_ls));
  my_1bit_mag_comp my_1bit_mag_comp_9 (
    .in_gt(my_1bit_mag_comp_8_out_gt), .in_eq(my_1bit_mag_comp_8_out_eq), .in_ls(my_1bit_mag_comp_8_out_ls),
    .input1(input1[7]), .input2(input2[7]), .out_gt(my_1bit_mag_comp_9_out_gt),
    .out_eq(my_1bit_mag_comp_9_out_eq), .out_ls(my_1bit_mag_comp_9_out_ls));
  my_1bit_mag_comp my_1bit_mag_comp_10 (
    .in_gt(my_1bit_mag_comp_9_out_gt), .in_eq(my_1bit_mag_comp_9_out_eq), .in_ls(my_1bit_mag_comp_9_out_ls),
    .input1(input1[6]), .input2(input2[6]), .out_gt(my_1bit_mag_comp_10_out_gt),
    .out_eq(my_1bit_mag_comp_10_out_eq), .out_ls(my_1bit_mag_comp_10_out_ls));
  my_1bit_mag_comp my_1bit_mag_comp_11 (
    .in_gt(my_1bit_mag_comp_10_out_gt), .in_eq(my_1bit_mag_comp_10_out_eq),
    .in_ls(my_1bit_mag_comp_10_out_ls), .input1(input1[5]), .input2(input2[5]),
    .out_gt(my_1bit_mag_comp_11_out_gt), .out_eq(my_1bit_mag_comp_11_out_eq),
    .out_ls(my_1bit_mag_comp_11_out_ls));
  my_1bit_mag_comp my_1bit_mag_comp_12 (
    .in_gt(my_1bit_mag_comp_11_out_gt), .in_eq(my_1bit_mag_comp_11_out_eq),
    .in_ls(my_1bit_mag_comp_11_out_ls), .input1(input1[4]), .input2(input2[4]),
    .out_gt(my_1bit_mag_comp_12_out_gt), .out_eq(my_1bit_mag_comp_12_out_eq),
    .out_ls(my_1bit_mag_comp_12_out_ls));
  my_1bit_mag_comp my_1bit_mag_comp_13 (
    .in_gt(my_1bit_mag_comp_12_out_gt), .in_eq(my_1bit_mag_comp_12_out_eq),
    .in_ls(my_1bit_mag_comp_12_out_ls), .input1(input1[3]), .input2(input2[3]),
    .out_gt(my_1bit_mag_comp_13_out_gt), .out_eq(my_1bit_mag_comp_13_out_eq),
    .out_ls(my_1bit_mag_comp_13_out_ls));
  my_1bit_mag_comp my_1bit_mag_comp_14 (
    .in_gt(my_1bit_mag_comp_13_out_gt), .in_eq(my_1bit_mag_comp_13_out_eq),
    .in_ls(my_1bit_mag_comp_13_out_ls), .input1(input1[2]), .input2(input2[2]),
    .out_gt(my_1bit_mag_comp_14_out_gt), .out_eq(my_1bit_mag_comp_14_out_eq),
    .out_ls(my_1bit_mag_comp_14_out_ls));
  my_1bit_mag_comp my_1bit_mag_comp_15 (
    .in_gt(my_1bit_mag_comp_14_out_gt), .in_eq(my_1bit_mag_comp_14_out_eq),
    .in_ls(my_1bit_mag_comp_14_out_ls), .input1(input1[1]), .input2(input2[1]),
    .out_gt(my_1bit_mag_comp_15_out_gt), .out_eq(my_1bit_mag_comp_15_out_eq),
    .out_ls(my_1bit_mag_comp_15_out_ls));
  my_1bit_mag_comp my_1bit_mag_comp_16 (
    .in_gt(my_1bit_mag_comp_15_out_gt), .in_eq(my_1bit_mag_comp_15_out_eq),
    .in_ls(my_1bit_mag_comp_15_out_ls), .input1(input1[0]), .input2(input2[0]), .out_gt(gt), .out_eq(eq),
    .out_ls(ls));

  assign input2[15] = input1[15];
endmodule

module my_program_counter (
  input  [15:0] jump_adress,
  input  if_0_add_1_else_jump,
  input  enable,
  input  clock,
  output [15:0] \output 
);

  wire my_2_1_1bit_mux_1_output, my_2_1_1bit_mux_2_output, my_2_1_1bit_mux_3_output,
       my_2_1_1bit_mux_4_output, my_2_1_1bit_mux_5_output, my_2_1_1bit_mux_6_output,
       my_2_1_1bit_mux_7_output, my_2_1_1bit_mux_8_output, my_2_1_1bit_mux_9_output,
       my_2_1_1bit_mux_10_output, my_2_1_1bit_mux_11_output, my_2_1_1bit_mux_12_output,
       my_2_1_1bit_mux_13_output, my_2_1_1bit_mux_14_output, my_2_1_1bit_mux_15_output,
       my_2_1_1bit_mux_16_output;
  wire [15:0] my_2_1_16bit_mux_1_output, my_16bit_fadder_1_output;

  my_2_1_1bit_mux my_2_1_1bit_mux_1 (
    .input1(my_2_1_16bit_mux_1_output[0]), .input2(\output [0]), .selector(1'b0),
    .\output (my_2_1_1bit_mux_1_output));
  D_Flip_Flop d_ff_1 (
    .clk(clock), .D(my_2_1_1bit_mux_1_output), .Q(\output [0]), .en(enable));  // open: Qn, preset, reset
  my_2_1_1bit_mux my_2_1_1bit_mux_2 (
    .input1(my_2_1_16bit_mux_1_output[1]), .input2(\output [1]), .selector(1'b0),
    .\output (my_2_1_1bit_mux_2_output));
  my_2_1_1bit_mux my_2_1_1bit_mux_3 (
    .input1(my_2_1_16bit_mux_1_output[2]), .input2(\output [2]), .selector(1'b0),
    .\output (my_2_1_1bit_mux_3_output));
  D_Flip_Flop d_ff_2 (
    .clk(clock), .D(my_2_1_1bit_mux_2_output), .Q(\output [1]), .en(enable));  // open: Qn, preset, reset
  my_2_1_1bit_mux my_2_1_1bit_mux_4 (
    .input1(my_2_1_16bit_mux_1_output[3]), .input2(\output [3]), .selector(1'b0),
    .\output (my_2_1_1bit_mux_4_output));
  D_Flip_Flop d_ff_3 (
    .clk(clock), .D(my_2_1_1bit_mux_3_output), .Q(\output [2]), .en(enable));  // open: Qn, preset, reset
  D_Flip_Flop d_ff_4 (
    .clk(clock), .D(my_2_1_1bit_mux_4_output), .Q(\output [3]), .en(enable));  // open: Qn, preset, reset
  my_2_1_1bit_mux my_2_1_1bit_mux_5 (
    .input1(my_2_1_16bit_mux_1_output[4]), .input2(\output [4]), .selector(1'b0),
    .\output (my_2_1_1bit_mux_5_output));
  D_Flip_Flop d_ff_5 (
    .clk(clock), .D(my_2_1_1bit_mux_5_output), .Q(\output [4]), .en(enable));  // open: Qn, preset, reset
  my_2_1_1bit_mux my_2_1_1bit_mux_6 (
    .input1(my_2_1_16bit_mux_1_output[5]), .input2(\output [5]), .selector(1'b0),
    .\output (my_2_1_1bit_mux_6_output));
  my_2_1_1bit_mux my_2_1_1bit_mux_7 (
    .input1(my_2_1_16bit_mux_1_output[6]), .input2(\output [6]), .selector(1'b0),
    .\output (my_2_1_1bit_mux_7_output));
  D_Flip_Flop d_ff_6 (
    .clk(clock), .D(my_2_1_1bit_mux_6_output), .Q(\output [5]), .en(enable));  // open: Qn, preset, reset
  my_16bit_fadder my_16bit_fadder_1 (
    .a15_a0(16'h1), .b15_b0(\output ), .cary_in(1'b0), .\output (my_16bit_fadder_1_output));  // open: cary_out
  my_2_1_16bit_mux my_2_1_16bit_mux_1 (
    .input1(my_16bit_fadder_1_output), .input2(jump_adress), .\output (my_2_1_16bit_mux_1_output),
    .selector(if_0_add_1_else_jump));
  my_2_1_1bit_mux my_2_1_1bit_mux_8 (
    .input1(my_2_1_16bit_mux_1_output[7]), .input2(\output [7]), .selector(1'b0),
    .\output (my_2_1_1bit_mux_8_output));
  D_Flip_Flop d_ff_7 (
    .clk(clock), .D(my_2_1_1bit_mux_7_output), .Q(\output [6]), .en(enable));  // open: Qn, preset, reset
  D_Flip_Flop d_ff_8 (
    .clk(clock), .D(my_2_1_1bit_mux_8_output), .Q(\output [7]), .en(enable));  // open: Qn, preset, reset
  my_2_1_1bit_mux my_2_1_1bit_mux_9 (
    .input1(my_2_1_16bit_mux_1_output[8]), .input2(\output [8]), .selector(1'b0),
    .\output (my_2_1_1bit_mux_9_output));
  D_Flip_Flop d_ff_9 (
    .clk(clock), .D(my_2_1_1bit_mux_9_output), .Q(\output [8]), .en(enable));  // open: Qn, preset, reset
  my_2_1_1bit_mux my_2_1_1bit_mux_10 (
    .input1(my_2_1_16bit_mux_1_output[9]), .input2(\output [9]), .selector(1'b0),
    .\output (my_2_1_1bit_mux_10_output));
  my_2_1_1bit_mux my_2_1_1bit_mux_11 (
    .input1(my_2_1_16bit_mux_1_output[10]), .input2(\output [10]), .selector(1'b0),
    .\output (my_2_1_1bit_mux_11_output));
  D_Flip_Flop d_ff_10 (
    .clk(clock), .D(my_2_1_1bit_mux_10_output), .Q(\output [9]), .en(enable));  // open: Qn, preset, reset
  my_2_1_1bit_mux my_2_1_1bit_mux_12 (
    .input1(my_2_1_16bit_mux_1_output[11]), .input2(\output [11]), .selector(1'b0),
    .\output (my_2_1_1bit_mux_12_output));
  D_Flip_Flop d_ff_11 (
    .clk(clock), .D(my_2_1_1bit_mux_11_output), .Q(\output [10]), .en(enable));  // open: Qn, preset, reset
  D_Flip_Flop d_ff_12 (
    .clk(clock), .D(my_2_1_1bit_mux_12_output), .Q(\output [11]), .en(enable));  // open: Qn, preset, reset
  my_2_1_1bit_mux my_2_1_1bit_mux_13 (
    .input1(my_2_1_16bit_mux_1_output[12]), .input2(\output [12]), .selector(1'b0),
    .\output (my_2_1_1bit_mux_13_output));
  D_Flip_Flop d_ff_13 (
    .clk(clock), .D(my_2_1_1bit_mux_13_output), .Q(\output [12]), .en(enable));  // open: Qn, preset, reset
  my_2_1_1bit_mux my_2_1_1bit_mux_14 (
    .input1(my_2_1_16bit_mux_1_output[13]), .input2(\output [13]), .selector(1'b0),
    .\output (my_2_1_1bit_mux_14_output));
  my_2_1_1bit_mux my_2_1_1bit_mux_15 (
    .input1(my_2_1_16bit_mux_1_output[14]), .input2(\output [14]), .selector(1'b0),
    .\output (my_2_1_1bit_mux_15_output));
  D_Flip_Flop d_ff_14 (
    .clk(clock), .D(my_2_1_1bit_mux_14_output), .Q(\output [13]), .en(enable));  // open: Qn, preset, reset
  my_2_1_1bit_mux my_2_1_1bit_mux_16 (
    .input1(my_2_1_16bit_mux_1_output[15]), .input2(\output [15]), .selector(1'b0),
    .\output (my_2_1_1bit_mux_16_output));
  D_Flip_Flop d_ff_15 (
    .clk(clock), .D(my_2_1_1bit_mux_15_output), .Q(\output [14]), .en(enable));  // open: Qn, preset, reset
  D_Flip_Flop d_ff_16 (
    .clk(clock), .D(my_2_1_1bit_mux_16_output), .Q(\output [15]), .en(enable));  // open: Qn, preset, reset
endmodule

module ALU_Selector (
  input  \and ,
  input  add,
  input  \andı ,
  input  \addı ,
  output [1:0] selection
);

  wire and_2_out, not_1_out, not_2_out, or_1_out, or_2_out;
  wire [1:0] and_1_out;

  or or_1 (or_1_out, \and , \andı );
  or or_2 (or_2_out, add, \addı );
  not not_1 (not_1_out, or_2_out);
  not not_2 (not_2_out, or_1_out);
  and and_1 (and_1_out[0], or_1_out, not_1_out);
  and and_2 (and_2_out, not_2_out, or_2_out);
  or or_3 (and_1_out[1], and_1_out[0], and_2_out);
  assign selection = ~and_1_out;  // NOT_Gate not_3, 2 bits wide
endmodule

module my_12_t0_16_extender (
  input  [11:0] \input ,
  output [15:0] \output 
);


  assign \output  = {{5{\input [11]}}, \input [10:0]};
endmodule

module flag (
  input  \input ,
  input  enable,
  input  clk,
  output ouput
);

  D_Flip_Flop d_ff_1 (.clk(clk), .D(\input ), .Q(ouput), .en(enable));  // open: Qn, preset, reset
endmodule

module _1bit_substractor (
  input  a,
  input  b,
  input  wi,
  output s,
  output wo
);

  wire and_1_out, and_2_out, not_1_out, not_2_out, xor_1_out;

  not not_1 (not_1_out, a);
  and and_1 (and_1_out, not_1_out, b);
  or or_1 (wo, and_1_out, and_2_out);
  xor xor_1 (xor_1_out, a, b);
  not not_2 (not_2_out, xor_1_out);
  xor xor_2 (s, xor_1_out, wi);
  and and_2 (and_2_out, wi, not_2_out);
endmodule

module my_16bit_comparator (
  input  [15:0] input1,
  input  [15:0] input2,
  output cary_flag,
  output zero_flag
);

  wire n1bit_substractor_1_s, n1bit_substractor_2_s, n1bit_substractor_2_wo, n1bit_substractor_3_s,
       n1bit_substractor_3_wo, n1bit_substractor_4_s, n1bit_substractor_4_wo, n1bit_substractor_5_s,
       n1bit_substractor_5_wo, n1bit_substractor_6_s, n1bit_substractor_6_wo, n1bit_substractor_7_s,
       n1bit_substractor_7_wo, n1bit_substractor_8_s, n1bit_substractor_8_wo, n1bit_substractor_9_s,
       n1bit_substractor_9_wo, n1bit_substractor_10_s, n1bit_substractor_10_wo, n1bit_substractor_11_s,
       n1bit_substractor_11_wo, n1bit_substractor_12_s, n1bit_substractor_12_wo, n1bit_substractor_13_s,
       n1bit_substractor_13_wo, n1bit_substractor_14_s, n1bit_substractor_14_wo, n1bit_substractor_15_s,
       n1bit_substractor_15_wo, n1bit_substractor_16_s, n1bit_substractor_16_wo;

  _1bit_substractor u_1bit_substractor_1 (
    .a(input1[15]), .b(input2[15]), .wi(n1bit_substractor_2_wo), .wo(cary_flag), .s(n1bit_substractor_1_s));
  _1bit_substractor u_1bit_substractor_2 (
    .a(input1[14]), .b(input2[14]), .wi(n1bit_substractor_3_wo), .wo(n1bit_substractor_2_wo),
    .s(n1bit_substractor_2_s));
  _1bit_substractor u_1bit_substractor_3 (
    .a(input1[13]), .b(input2[13]), .wi(n1bit_substractor_4_wo), .wo(n1bit_substractor_3_wo),
    .s(n1bit_substractor_3_s));
  _1bit_substractor u_1bit_substractor_4 (
    .a(input1[12]), .b(input2[12]), .wi(n1bit_substractor_5_wo), .wo(n1bit_substractor_4_wo),
    .s(n1bit_substractor_4_s));
  _1bit_substractor u_1bit_substractor_5 (
    .a(input1[11]), .b(input2[11]), .wi(n1bit_substractor_6_wo), .wo(n1bit_substractor_5_wo),
    .s(n1bit_substractor_5_s));
  _1bit_substractor u_1bit_substractor_6 (
    .a(input1[10]), .b(input2[10]), .wi(n1bit_substractor_7_wo), .wo(n1bit_substractor_6_wo),
    .s(n1bit_substractor_6_s));
  _1bit_substractor u_1bit_substractor_7 (
    .a(input1[9]), .b(input2[9]), .wi(n1bit_substractor_8_wo), .wo(n1bit_substractor_7_wo),
    .s(n1bit_substractor_7_s));
  _1bit_substractor u_1bit_substractor_8 (
    .a(input1[8]), .b(input2[8]), .wi(n1bit_substractor_9_wo), .wo(n1bit_substractor_8_wo),
    .s(n1bit_substractor_8_s));
  _1bit_substractor u_1bit_substractor_9 (
    .a(input1[7]), .b(input2[7]), .wi(n1bit_substractor_10_wo), .wo(n1bit_substractor_9_wo),
    .s(n1bit_substractor_9_s));
  nor nor_1 (zero_flag, n1bit_substractor_1_s, n1bit_substractor_2_s, n1bit_substractor_3_s, n1bit_substractor_4_s, n1bit_substractor_5_s, n1bit_substractor_6_s, n1bit_substractor_7_s, n1bit_substractor_8_s, n1bit_substractor_9_s, n1bit_substractor_10_s, n1bit_substractor_11_s, n1bit_substractor_12_s, n1bit_substractor_13_s, n1bit_substractor_14_s, n1bit_substractor_15_s, n1bit_substractor_16_s);
  _1bit_substractor u_1bit_substractor_10 (
    .a(input1[6]), .b(input2[6]), .wi(n1bit_substractor_11_wo), .wo(n1bit_substractor_10_wo),
    .s(n1bit_substractor_10_s));
  _1bit_substractor u_1bit_substractor_11 (
    .a(input1[5]), .b(input2[5]), .wi(n1bit_substractor_12_wo), .wo(n1bit_substractor_11_wo),
    .s(n1bit_substractor_11_s));
  _1bit_substractor u_1bit_substractor_12 (
    .a(input1[4]), .b(input2[4]), .wi(n1bit_substractor_13_wo), .wo(n1bit_substractor_12_wo),
    .s(n1bit_substractor_12_s));
  _1bit_substractor u_1bit_substractor_13 (
    .a(input1[3]), .b(input2[3]), .wi(n1bit_substractor_14_wo), .wo(n1bit_substractor_13_wo),
    .s(n1bit_substractor_13_s));
  _1bit_substractor u_1bit_substractor_14 (
    .a(input1[2]), .b(input2[2]), .wi(n1bit_substractor_15_wo), .wo(n1bit_substractor_14_wo),
    .s(n1bit_substractor_14_s));
  _1bit_substractor u_1bit_substractor_15 (
    .a(input1[1]), .b(input2[1]), .wi(n1bit_substractor_16_wo), .wo(n1bit_substractor_15_wo),
    .s(n1bit_substractor_15_s));
  _1bit_substractor u_1bit_substractor_16 (
    .a(input1[0]), .b(input2[0]), .wi(1'b0), .wo(n1bit_substractor_16_wo), .s(n1bit_substractor_16_s));
endmodule

module my_control_unit (
  input  [15:0] \input ,
  output [2:0] src2,
  output [2:0] src1,
  output [2:0] src1_2,
  output [15:0] immediate,
  output [9:0] ram_adress,
  output [15:0] jump_adress,
  output AND,
  output ADD,
  output ST,
  output LD,
  output ADDI,
  output ANDI,
  output CMP,
  output JUMP,
  output JE,
  output JA,
  output JAE,
  output JBE,
  output JB
);

  my_12_t0_16_extender extender (.\input (\input [11:0]), .\output (jump_adress));
  my_4_16_16bit_decoder my_4_16_16bit_decoder_1 (
    .\and (AND), .add(ADD), .st(LD), .\andı (ST), .\addı (ANDI), .cmp(ADDI), .jump(CMP), .je(JUMP), .ja(JE),
    .jb(JA), .jbe(JB), .jae(JBE), .\null (JAE), ._4_0(\input [15:12]), .enable(1'b1));  // open: ld, null_2, null_3
  my_9_to_10_extender extender_2 (.\input (\input [8:0]), .\output (ram_adress));
  my_6_to16_extender extender_3 (.\input (\input [5:0]), .\output (immediate));

  assign src1 = \input [8:6];
  assign src1_2 = \input [11:9];
  assign src2 = \input [5:3];
endmodule
