// Logisim project project.circ as structural Verilog: 31 circuits, main circuit main
module main (
  input  in_1,
  input  jump,
  input  in_3,
  input  in_4,
  input  in_5,
  output [15:0] out_6
);

  wire and_2_out, clock_1_out, my_2_1_1bit_mux_1_output, my_4_16_16bit_decoder_1_add,
       \my_4_16_16bit_decoder_1_addı , my_4_16_16bit_decoder_1_and, \my_4_16_16bit_decoder_1_andı ,
       my_4_16_16bit_decoder_1_ld, my_4_16_16bit_decoder_1_st, not_1_out, not_2_out, or_1_out, or_2_out,
       or_3_out, or_4_out, or_5_out;
  wire [1:0] and_1_out, not_3_out;
  wire [8:0] my_4_16_16bit_decoder_1_jump;
  wire [9:0] extender_2_output, my_mux_3_output;
  wire [15:0] extender_output, my_ALU_output, my_mux_2_output, my_mux_output, PC_output, ram_1_data,
       registers_output1, registers_output2;

  Program_Counter PC (
    .if_0_add_1_else_jump(jump), .enable(in_4), .clk(my_2_1_1bit_mux_1_output), .\output (PC_output));  // open: jump_adress
  my_2_1_1bit_mux my_2_1_1bit_mux_1 (
    .input1(1'b0), .input2(clock_1_out), .selector(in_1), .\output (my_2_1_1bit_mux_1_output));
  my_4_16_16bit_decoder my_4_16_16bit_decoder_1 (
    .\and (my_4_16_16bit_decoder_1_and), .add(my_4_16_16bit_decoder_1_add), .ld(my_4_16_16bit_decoder_1_ld),
    .st(my_4_16_16bit_decoder_1_st), .\andı (\my_4_16_16bit_decoder_1_andı ),
    .\addı (\my_4_16_16bit_decoder_1_addı ), .jump(my_4_16_16bit_decoder_1_jump[0]),
    .je(my_4_16_16bit_decoder_1_jump[1]), .ja(my_4_16_16bit_decoder_1_jump[2]),
    .jb(my_4_16_16bit_decoder_1_jump[3]), .jbe(my_4_16_16bit_decoder_1_jump[4]),
    .jae(my_4_16_16bit_decoder_1_jump[5]), .\null (my_4_16_16bit_decoder_1_jump[6]),
    .null_2(my_4_16_16bit_decoder_1_jump[7]), .null_3(my_4_16_16bit_decoder_1_jump[8]), ._4_0(out_6[15:12]),
    .enable(in_4));  // open: cmp
  ROM #(.addrWidth(16), .dataWidth(16)) rom_1 (.addr(PC_output), .data(out_6), .sel(in_4));
  registers registers (
    .storeNumber(out_6[11:9]), .clk(in_3), .\input (my_mux_2_output), .enable(in_5),
    .adress_output1(out_6[8:6]), .adress_output2(out_6[5:3]), .output1(registers_output1),
    .output2(registers_output2), .load(or_1_out));
  or or_1 (or_1_out, my_4_16_16bit_decoder_1_and, my_4_16_16bit_decoder_1_add, my_4_16_16bit_decoder_1_ld, \my_4_16_16bit_decoder_1_andı , \my_4_16_16bit_decoder_1_addı );
  Clock clock_1 (.out(clock_1_out));
  my_2_1_16bit_mux my_mux (
    .input1(registers_output2), .input2(extender_output), .selector(or_2_out), .\output (my_mux_output));
  my_2_1_16bit_mux my_mux_2 (
    .input1(my_ALU_output), .input2(ram_1_data), .selector(my_4_16_16bit_decoder_1_ld),
    .\output (my_mux_2_output));
  or or_2 (or_2_out, \my_4_16_16bit_decoder_1_addı , \my_4_16_16bit_decoder_1_andı );
  or or_3 (or_3_out, my_4_16_16bit_decoder_1_and, \my_4_16_16bit_decoder_1_andı );
  or or_4 (or_4_out, my_4_16_16bit_decoder_1_add, \my_4_16_16bit_decoder_1_addı );
  or or_5 (or_5_out, my_4_16_16bit_decoder_1_st, my_4_16_16bit_decoder_1_ld);
  not not_1 (not_1_out, or_3_out);
  not not_2 (not_2_out, or_4_out);
  my_6_to16_extender extender (.\input (out_6[5:0]), .\output (extender_output));
  and and_1 (and_1_out[0], or_3_out, not_2_out);
  and and_2 (and_2_out, not_1_out, or_4_out);
  my_2_1_10bit_mux my_mux_3 (
    .\output (my_mux_3_output), .input1(extender_2_output), .input2(out_6[9:0]), .selector(or_5_out));
  or or_6 (and_1_out[1], and_1_out[0], and_2_out);
  my_9_to_10_extender extender_2 (.\input (out_6[8:0]), .\output (extender_2_output));
  assign not_3_out = ~and_1_out;  // NOT_Gate not_3, 2 bits wide
  my_ALU my_ALU (.input1(registers_output1), .input2(my_mux_output), .\output (my_ALU_output), .opcode(not_3_out));
  RAM #(.addrWidth(10), .dataWidth(16), .bus("separate")) ram_1 (
    .addr(my_mux_3_output), .din(registers_output1), .data(ram_1_data), .str(my_4_16_16bit_decoder_1_st),
    .ld(my_4_16_16bit_decoder_1_ld), .clr(in_3));  // open: sel, clk

  // Notes on the sheet:
  //   contents of rom_1 (hex, n*v repeats v):
  //   5015 0 100 1111 11
endmodule

module my_d_latch (
  input  enable,
  input  \input ,
  input  clk,
  output \output 
);

  wire and_1_out, and_2_out, my_2_1_1bit_mux_1_output, nor_1_out, not_1_out;

  my_2_1_1bit_mux my_2_1_1bit_mux_1 (
    .input1(1'b0), .input2(\input ), .selector(enable), .\output (my_2_1_1bit_mux_1_output));
  not not_1 (not_1_out, my_2_1_1bit_mux_1_output);
  and and_1 (and_1_out, my_2_1_1bit_mux_1_output, clk);
  and and_2 (and_2_out, clk, not_1_out);
  nor nor_1 (nor_1_out, and_1_out, \output );
  nor nor_2 (\output , nor_1_out, and_2_out);
endmodule

module my_d_flipflop (
  input  enable,
  input  \input ,
  input  clk,
  output \output 
);

  wire d_latch_output, not_1_out;

  not not_1 (not_1_out, clk);
  my_d_latch d_latch (.\input (\input ), .clk(not_1_out), .enable(enable), .\output (d_latch_output));
  my_d_latch d_latch_2 (.\input (d_latch_output), .clk(clk), .enable(enable), .\output (\output ));
endmodule

module my_16bit_reg (
  input  [15:0] \input ,
  input  load,
  input  enable,
  input  clk,
  output [15:0] \output 
);

  wire my_2_1_1bit_mux_1_output, my_2_1_1bit_mux_2_output, my_2_1_1bit_mux_3_output,
       my_2_1_1bit_mux_4_output, my_2_1_1bit_mux_5_output, my_2_1_1bit_mux_6_output,
       my_2_1_1bit_mux_7_output, my_2_1_1bit_mux_8_output, my_2_1_1bit_mux_9_output,
       my_2_1_1bit_mux_10_output, my_2_1_1bit_mux_11_output, my_2_1_1bit_mux_12_output,
       my_2_1_1bit_mux_13_output, my_2_1_1bit_mux_14_output, my_2_1_1bit_mux_15_output,
       my_2_1_1bit_mux_16_output, not_1_out;

  not not_1 (not_1_out, load);
  my_2_1_1bit_mux my_2_1_1bit_mux_1 (
    .input1(\input [0]), .input2(\output [0]), .selector(not_1_out), .\output (my_2_1_1bit_mux_1_output));
  my_2_1_1bit_mux my_2_1_1bit_mux_2 (
    .input1(\input [1]), .input2(\output [1]), .selector(not_1_out), .\output (my_2_1_1bit_mux_2_output));
  my_d_flipflop my_d_flipflop_1 (
    .\input (my_2_1_1bit_mux_2_output), .clk(clk), .\output (\output [1]), .enable(enable));
  my_d_flipflop my_d_flipflop_2 (
    .\input (my_2_1_1bit_mux_1_output), .clk(clk), .\output (\output [0]), .enable(enable));
  my_2_1_1bit_mux my_2_1_1bit_mux_3 (
    .input1(\input [2]), .input2(\output [2]), .selector(not_1_out), .\output (my_2_1_1bit_mux_3_output));
  my_d_flipflop my_d_flipflop_3 (
    .\input (my_2_1_1bit_mux_3_output), .clk(clk), .\output (\output [2]), .enable(enable));
  my_2_1_1bit_mux my_2_1_1bit_mux_4 (
    .input1(\input [3]), .input2(\output [3]), .selector(not_1_out), .\output (my_2_1_1bit_mux_4_output));
  my_d_flipflop my_d_flipflop_4 (
    .\input (my_2_1_1bit_mux_4_output), .clk(clk), .\output (\output [3]), .enable(enable));
  my_2_1_1bit_mux my_2_1_1bit_mux_5 (
    .input1(\input [4]), .input2(\output [4]), .selector(not_1_out), .\output (my_2_1_1bit_mux_5_output));
  my_d_flipflop my_d_flipflop_5 (
    .\input (my_2_1_1bit_mux_5_output), .clk(clk), .\output (\output [4]), .enable(enable));
  my_2_1_1bit_mux my_2_1_1bit_mux_6 (
    .input1(\input [5]), .input2(\output [5]), .selector(not_1_out), .\output (my_2_1_1bit_mux_6_output));
  my_d_flipflop my_d_flipflop_6 (
    .\input (my_2_1_1bit_mux_6_output), .clk(clk), .\output (\output [5]), .enable(enable));
  my_2_1_1bit_mux my_2_1_1bit_mux_7 (
    .input1(\input [6]), .input2(\output [6]), .selector(not_1_out), .\output (my_2_1_1bit_mux_7_output));
  my_d_flipflop my_d_flipflop_7 (
    .\input (my_2_1_1bit_mux_7_output), .clk(clk), .\output (\output [6]), .enable(enable));
  my_2_1_1bit_mux my_2_1_1bit_mux_8 (
    .input1(\input [7]), .input2(\output [7]), .selector(not_1_out), .\output (my_2_1_1bit_mux_8_output));
  my_d_flipflop my_d_flipflop_8 (
    .\input (my_2_1_1bit_mux_8_output), .clk(clk), .\output (\output [7]), .enable(enable));
  my_2_1_1bit_mux my_2_1_1bit_mux_9 (
    .input1(\input [8]), .input2(\output [8]), .selector(not_1_out), .\output (my_2_1_1bit_mux_9_output));
  my_d_flipflop my_d_flipflop_9 (
    .\input (my_2_1_1bit_mux_9_output), .clk(clk), .\output (\output [8]), .enable(enable));
  my_2_1_1bit_mux my_2_1_1bit_mux_10 (
    .input1(\input [9]), .input2(\output [9]), .selector(not_1_out), .\output (my_2_1_1bit_mux_10_output));
  my_2_1_1bit_mux my_2_1_1bit_mux_11 (
    .input1(\input [10]), .input2(\output [10]), .selector(not_1_out), .\output (my_2_1_1bit_mux_11_output));
  my_d_flipflop my_d_flipflop_10 (
    .\input (my_2_1_1bit_mux_10_output), .clk(clk), .\output (\output [9]), .enable(enable));
  my_d_flipflop my_d_flipflop_11 (
    .\input (my_2_1_1bit_mux_11_output), .clk(clk), .\output (\output [10]), .enable(enable));
  my_2_1_1bit_mux my_2_1_1bit_mux_12 (
    .input1(\input [11]), .input2(\output [11]), .selector(not_1_out), .\output (my_2_1_1bit_mux_12_output));
  my_d_flipflop my_d_flipflop_12 (
    .\input (my_2_1_1bit_mux_12_output), .clk(clk), .\output (\output [11]), .enable(enable));
  my_2_1_1bit_mux my_2_1_1bit_mux_13 (
    .input1(\input [12]), .input2(\output [12]), .selector(not_1_out), .\output (my_2_1_1bit_mux_13_output));
  my_d_flipflop my_d_flipflop_13 (
    .\input (my_2_1_1bit_mux_13_output), .clk(clk), .\output (\output [12]), .enable(enable));
  my_2_1_1bit_mux my_2_1_1bit_mux_14 (
    .input1(\input [13]), .input2(\output [13]), .selector(not_1_out), .\output (my_2_1_1bit_mux_14_output));
  my_d_flipflop my_d_flipflop_14 (
    .\input (my_2_1_1bit_mux_14_output), .clk(clk), .\output (\output [13]), .enable(enable));
  my_2_1_1bit_mux my_2_1_1bit_mux_15 (
    .input1(\input [14]), .input2(\output [14]), .selector(not_1_out), .\output (my_2_1_1bit_mux_15_output));
  my_d_flipflop my_d_flipflop_15 (
    .\input (my_2_1_1bit_mux_15_output), .clk(clk), .\output (\output [14]), .enable(enable));
  my_2_1_1bit_mux my_2_1_1bit_mux_16 (
    .input1(\input [15]), .input2(\output [15]), .selector(not_1_out), .\output (my_2_1_1bit_mux_16_output));
  my_d_flipflop my_d_flipflop_16 (
    .\input (my_2_1_1bit_mux_16_output), .clk(clk), .\output (\output [15]), .enable(enable));
endmodule

module my_3_8_decoder (
  input  in_1,
  input  in_2,
  input  in_3,
  input  load,
  output out_5,
  output out_6,
  output out_7,
  output out_8,
  output out_9,
  output out_10,
  output out_11,
  output out_12
);

  wire not_1_out, not_2_out, not_3_out, not_4_out, not_5_out, not_6_out, not_7_out, not_8_out, not_9_out,
       not_10_out, not_11_out, not_12_out;

  not not_1 (not_1_out, in_1);
  not not_2 (not_2_out, in_2);
  not not_3 (not_3_out, in_3);
  not not_4 (not_4_out, in_1);
  not not_5 (not_5_out, in_2);
  not not_6 (not_6_out, in_1);
  not not_7 (not_7_out, in_3);
  not not_8 (not_8_out, in_1);
  not not_9 (not_9_out, in_2);
  not not_10 (not_10_out, in_3);
  not not_11 (not_11_out, in_2);
  not not_12 (not_12_out, in_3);
  and and_1 (out_5, not_1_out, not_2_out, load, not_3_out);
  and and_2 (out_6, not_4_out, not_5_out, load, in_3);
  and and_3 (out_7, not_6_out, in_2, load, not_7_out);
  and and_4 (out_8, not_8_out, in_2, load, in_3);
  and and_5 (out_9, in_1, not_9_out, load, not_10_out);
  and and_6 (out_10, in_1, not_11_out, load, in_3);
  and and_7 (out_11, in_1, in_2, load, not_12_out);
  and and_8 (out_12, in_1, in_2, load, in_3);
endmodule

module my_2_1_1bit_mux (
  input  input1,
  input  input2,
  input  selector,
  output \output 
);

  wire and_1_out, and_2_out, not_1_out;

  not not_1 (not_1_out, selector);
  and and_1 (and_1_out, input1, not_1_out);
  and and_2 (and_2_out, input2, selector);
  or or_1 (\output , and_1_out, and_2_out);
endmodule

module registers (
  input  [15:0] \input ,
  input  enable,
  input  [2:0] adress_output1,
  input  [2:0] storeNumber,
  input  [2:0] adress_output2,
  input  clk,
  input  load,
  output [15:0] output1,
  output [15:0] output2
);

  wire my_3_8_decoder_1_out_5, my_3_8_decoder_1_out_6, my_3_8_decoder_1_out_7, my_3_8_decoder_1_out_8,
       my_3_8_decoder_1_out_9, my_3_8_decoder_1_out_10, my_3_8_decoder_1_out_11, my_3_8_decoder_1_out_12;
  wire [15:0] my_16bit_reg_1_output, my_16bit_reg_2_output, my_16bit_reg_3_output, my_16bit_reg_4_output,
       R0_3_output, R0_output, R3_output, undriven;

  my_3_8_decoder my_3_8_decoder_1 (
    .in_1(storeNumber[2]), .in_2(storeNumber[1]), .in_3(storeNumber[0]), .load(load),
    .out_5(my_3_8_decoder_1_out_5), .out_6(my_3_8_decoder_1_out_6), .out_7(my_3_8_decoder_1_out_7),
    .out_8(my_3_8_decoder_1_out_8), .out_9(my_3_8_decoder_1_out_9), .out_10(my_3_8_decoder_1_out_10),
    .out_11(my_3_8_decoder_1_out_11), .out_12(my_3_8_decoder_1_out_12));
  my_16bit_reg R0 (.load(my_3_8_decoder_1_out_5), .enable(enable), .clk(clk), .\input (\input ), .\output (R0_output));
  my_16bit_reg R0_2 (.load(my_3_8_decoder_1_out_6), .enable(enable), .clk(clk), .\input (\input ));  // open: output
  my_16bit_reg R0_3 (
    .load(my_3_8_decoder_1_out_7), .enable(enable), .clk(clk), .\input (\input ), .\output (R0_3_output));
  my_16bit_reg R3 (.load(my_3_8_decoder_1_out_8), .enable(enable), .clk(clk), .\input (\input ), .\output (R3_output));
  my_16bit_reg my_16bit_reg_1 (
    .load(my_3_8_decoder_1_out_9), .enable(enable), .clk(clk), .\input (\input ),
    .\output (my_16bit_reg_1_output));
  my_16bit_reg my_16bit_reg_2 (
    .load(my_3_8_decoder_1_out_10), .enable(enable), .clk(clk), .\input (\input ),
    .\output (my_16bit_reg_2_output));
  my_16bit_reg my_16bit_reg_3 (
    .load(my_3_8_decoder_1_out_11), .enable(enable), .clk(clk), .\input (\input ),
    .\output (my_16bit_reg_3_output));
  my_16bit_reg my_16bit_reg_4 (
    .load(my_3_8_decoder_1_out_12), .enable(enable), .clk(clk), .\input (\input ),
    .\output (my_16bit_reg_4_output));
  my_8_1_16bit_mux my_8_1_16bit_mux_1 (
    .in_1(R0_output), .in_2(undriven), .in_3(R0_3_output), .in_4(R3_output), .in_5(my_16bit_reg_1_output),
    .in_6(my_16bit_reg_2_output), .in_7(my_16bit_reg_3_output), .in_8(my_16bit_reg_4_output),
    .in_9(adress_output1[2]), .in_10(adress_output1[1]), .in_11(adress_output1[0]), .out_12(output1));
  my_8_1_16bit_mux my_8_1_16bit_mux_2 (
    .in_1(R0_output), .in_2(undriven), .in_3(R0_3_output), .in_4(R3_output), .in_5(my_16bit_reg_1_output),
    .in_6(my_16bit_reg_2_output), .in_7(my_16bit_reg_3_output), .in_8(my_16bit_reg_4_output),
    .in_9(adress_output2[2]), .in_10(adress_output2[1]), .in_11(adress_output2[0]), .out_12(output2));
endmodule

module my_2_4_decoder (
  input  in_1,
  input  in_2,
  input  in_3,
  output out_4,
  output out_5,
  output out_6,
  output out_7
);

  wire not_1_out, not_2_out, not_3_out, not_4_out;

  not not_1 (not_1_out, in_1);
  not not_2 (not_2_out, in_2);
  not not_3 (not_3_out, in_1);
  not not_4 (not_4_out, in_2);
  and and_1 (out_4, not_1_out, not_2_out, in_3);
  and and_2 (out_5, not_3_out, in_2, in_3);
  and and_3 (out_6, in_1, not_4_out, in_3);
  and and_4 (out_7, in_1, in_2, in_3);
endmodule

module my_8_1_16bit_mux (
  input  [15:0] in_1,
  input  [15:0] in_2,
  input  [15:0] in_3,
  input  [15:0] in_4,
  input  [15:0] in_5,
  input  [15:0] in_6,
  input  [15:0] in_7,
  input  [15:0] in_8,
  input  in_9,
  input  in_10,
  input  in_11,
  output [15:0] out_12
);

  wire [15:0] and_1_out, and_2_out, and_3_out, and_4_out, and_5_out, and_6_out, and_7_out, and_8_out,
       my_1_16_extender_1_output, my_1_16_extender_2_output, my_1_16_extender_3_output, not_1_out, not_2_out,
       not_3_out, not_4_out, not_5_out, not_6_out, not_7_out, not_8_out, not_9_out, not_10_out, not_11_out,
       not_12_out;

  my_1_16_extender my_1_16_extender_1 (.\input (in_9), .\output (my_1_16_extender_1_output));
  my_1_16_extender my_1_16_extender_2 (.\input (in_10), .\output (my_1_16_extender_2_output));
  assign not_1_out = ~my_1_16_extender_1_output;  // NOT_Gate not_1, 16 bits wide
  assign not_2_out = ~my_1_16_extender_2_output;  // NOT_Gate not_2, 16 bits wide
  assign not_3_out = ~my_1_16_extender_3_output;  // NOT_Gate not_3, 16 bits wide
  assign not_4_out = ~my_1_16_extender_1_output;  // NOT_Gate not_4, 16 bits wide
  assign not_5_out = ~my_1_16_extender_2_output;  // NOT_Gate not_5, 16 bits wide
  assign not_6_out = ~my_1_16_extender_1_output;  // NOT_Gate not_6, 16 bits wide
  assign not_7_out = ~my_1_16_extender_3_output;  // NOT_Gate not_7, 16 bits wide
  assign not_8_out = ~my_1_16_extender_1_output;  // NOT_Gate not_8, 16 bits wide
  assign not_9_out = ~my_1_16_extender_2_output;  // NOT_Gate not_9, 16 bits wide
  assign not_10_out = ~my_1_16_extender_3_output;  // NOT_Gate not_10, 16 bits wide
  assign not_11_out = ~my_1_16_extender_2_output;  // NOT_Gate not_11, 16 bits wide
  assign not_12_out = ~my_1_16_extender_3_output;  // NOT_Gate not_12, 16 bits wide
  my_1_16_extender my_1_16_extender_3 (.\input (in_11), .\output (my_1_16_extender_3_output));
  assign and_1_out = in_1 & not_1_out & not_2_out & not_3_out;  // AND_Gate and_1, 16 bits wide
  assign and_2_out = in_2 & not_4_out & not_5_out & my_1_16_extender_3_output;  // AND_Gate and_2, 16 bits wide
  assign and_3_out = in_3 & not_6_out & my_1_16_extender_2_output & not_7_out;  // AND_Gate and_3, 16 bits wide
  assign and_4_out = in_4 & not_8_out & my_1_16_extender_2_output & my_1_16_extender_3_output;  // AND_Gate and_4, 16 bits wide
  assign and_5_out = in_5 & my_1_16_extender_1_output & not_9_out & not_10_out;  // AND_Gate and_5, 16 bits wide
  assign and_6_out = in_6 & my_1_16_extender_1_output & not_11_out & my_1_16_extender_3_output;  // AND_Gate and_6, 16 bits wide
  assign and_7_out = in_7 & my_1_16_extender_1_output & my_1_16_extender_2_output & not_12_out;  // AND_Gate and_7, 16 bits wide
  assign and_8_out = in_8 & my_1_16_extender_1_output & my_1_16_extender_2_output & my_1_16_extender_3_output;  // AND_Gate and_8, 16 bits wide
  assign out_12 = and_1_out | and_2_out | and_3_out | and_4_out | and_5_out | and_6_out | and_7_out | and_8_out;  // OR_Gate or_1, 16 bits wide
endmodule

module my_1_3_extender (
  input  in_1,
  output [2:0] out_2
);


  assign out_2 = {3{in_1}};
endmodule

module my_ALU (
  input  [15:0] input1,
  input  [15:0] input2,
  input  [1:0] opcode,
  output [15:0] \output 
);

  wire [15:0] and_1_out, my_16bit_fadder_1_output, or_1_out;

  assign and_1_out = input1 & input2;  // AND_Gate and_1, 16 bits wide
  my_16bit_fadder my_16bit_fadder_1 (
    .a15_a0(input2), .b15_b0(input1), .cary_in(1'b0), .\output (my_16bit_fadder_1_output));  // open: cary_out
  assign or_1_out = input1 | input2;  // OR_Gate or_1, 16 bits wide
  my_4_1_16bit_mux my_mux (
    ._0(and_1_out), ._1(my_16bit_fadder_1_output), ._2(or_1_out), .in_5(opcode), .out_6(\output ));  // open: _3
endmodule

module my_1_16_extender (
  input  \input ,
  output [15:0] \output 
);


  assign \output  = {16{\input }};
endmodule

module my_4_1_16bit_mux (
  input  [15:0] _0,
  input  [15:0] _1,
  input  [15:0] _2,
  input  [15:0] _3,
  input  [1:0] in_5,
  output [15:0] out_6
);

  wire [15:0] and_1_out, and_2_out, and_3_out, and_4_out, my_1_16_extender_1_output,
       my_1_16_extender_2_output, not_1_out, not_2_out, not_3_out, not_4_out;

  my_1_16_extender my_1_16_extender_1 (.\input (in_5[1]), .\output (my_1_16_extender_1_output));
  my_1_16_extender my_1_16_extender_2 (.\input (in_5[0]), .\output (my_1_16_extender_2_output));
  assign not_1_out = ~my_1_16_extender_1_output;  // NOT_Gate not_1, 16 bits wide
  assign not_2_out = ~my_1_16_extender_2_output;  // NOT_Gate not_2, 16 bits wide
  assign not_3_out = ~my_1_16_extender_1_output;  // NOT_Gate not_3, 16 bits wide
  assign not_4_out = ~my_1_16_extender_2_output;  // NOT_Gate not_4, 16 bits wide
  assign and_1_out = _0 & not_1_out & not_2_out;  // AND_Gate and_1, 16 bits wide
  assign and_2_out = _1 & not_3_out & my_1_16_extender_2_output;  // AND_Gate and_2, 16 bits wide
  assign and_3_out = _2 & my_1_16_extender_1_output & not_4_out;  // AND_Gate and_3, 16 bits wide
  assign and_4_out = _3 & my_1_16_extender_1_output & my_1_16_extender_2_output;  // AND_Gate and_4, 16 bits wide
  assign out_6 = and_1_out | and_2_out | and_3_out | and_4_out;  // OR_Gate or_1, 16 bits wide
endmodule

module my_4_16_16bit_decoder (
  input  enable,
  input  [3:0] _4_0,
  output \and ,
  output add,
  output ld,
  output st,
  output \andı ,
  output \addı ,
  output cmp,
  output jump,
  output je,
  output ja,
  output jb,
  output jbe,
  output jae,
  output \null ,
  output null_2,
  output null_3
);

  wire not_1_out, not_2_out, not_3_out, not_4_out, not_5_out, not_6_out, not_7_out, not_8_out, not_9_out,
       not_10_out, not_11_out, not_12_out, not_13_out, not_14_out, not_15_out, not_16_out, not_17_out,
       not_18_out, not_19_out, not_20_out, not_21_out, not_22_out, not_23_out, not_24_out, not_25_out,
       not_26_out, not_27_out, not_28_out, not_29_out, not_30_out, not_31_out, not_32_out;

  not not_1 (not_1_out, _4_0[3]);
  not not_2 (not_2_out, _4_0[2]);
  and and_1 (\and , not_1_out, not_2_out, not_6_out, not_3_out, enable);
  not not_3 (not_3_out, _4_0[0]);
  not not_4 (not_4_out, _4_0[2]);
  not not_5 (not_5_out, _4_0[3]);
  not not_6 (not_6_out, _4_0[1]);
  and and_2 (add, not_5_out, not_4_out, not_8_out, _4_0[0], enable);
  not not_7 (not_7_out, _4_0[2]);
  not not_8 (not_8_out, _4_0[1]);
  not not_9 (not_9_out, _4_0[3]);
  and and_3 (ld, not_9_out, not_7_out, _4_0[1], not_11_out, enable);
  not not_10 (not_10_out, _4_0[3]);
  not not_11 (not_11_out, _4_0[0]);
  not not_12 (not_12_out, _4_0[2]);
  and and_4 (st, not_10_out, not_12_out, _4_0[1], _4_0[0], enable);
  and and_5 (\andı , not_13_out, _4_0[2], not_14_out, not_17_out, enable);
  not not_13 (not_13_out, _4_0[3]);
  not not_14 (not_14_out, _4_0[1]);
  and and_6 (\addı , not_15_out, _4_0[2], not_16_out, _4_0[0], enable);
  not not_15 (not_15_out, _4_0[3]);
  not not_16 (not_16_out, _4_0[1]);
  not not_17 (not_17_out, _4_0[0]);
  and and_7 (cmp, not_18_out, _4_0[2], _4_0[1], not_20_out, enable);
  not not_18 (not_18_out, _4_0[3]);
  and and_8 (jump, not_19_out, _4_0[2], _4_0[1], _4_0[0], enable);
  not not_19 (not_19_out, _4_0[3]);
  not not_20 (not_20_out, _4_0[0]);
  and and_9 (je, _4_0[3], not_22_out, not_23_out, not_21_out, enable);
  not not_21 (not_21_out, _4_0[0]);
  not not_22 (not_22_out, _4_0[2]);
  not not_23 (not_23_out, _4_0[1]);
  and and_10 (ja, _4_0[3], not_24_out, not_25_out, _4_0[0], enable);
  not not_24 (not_24_out, _4_0[2]);
  not not_25 (not_25_out, _4_0[1]);
  and and_11 (jb, _4_0[3], not_26_out, _4_0[1], not_27_out, enable);
  not not_26 (not_26_out, _4_0[2]);
  not not_27 (not_27_out, _4_0[0]);
  and and_12 (jbe, _4_0[3], not_28_out, _4_0[1], _4_0[0], enable);
  not not_28 (not_28_out, _4_0[2]);
  and and_13 (jae, _4_0[3], _4_0[2], not_29_out, not_30_out, enable);
  not not_29 (not_29_out, _4_0[1]);
  not not_30 (not_30_out, _4_0[0]);
  and and_14 (\null , _4_0[3], _4_0[2], not_31_out, _4_0[0], enable);
  not not_31 (not_31_out, _4_0[1]);
  and and_15 (null_2, _4_0[3], _4_0[2], _4_0[1], not_32_out, enable);
  not not_32 (not_32_out, _4_0[0]);
  and and_16 (null_3, _4_0[3], _4_0[2], _4_0[1], _4_0[0], enable);
endmodule

module my_1bit_fadder (
  input  cary_in,
  input  b,
  input  a,
  output cary_out,
  output s
);

  wire and_1_out, and_2_out, and_3_out;

  and and_1 (and_1_out, a, b);
  and and_2 (and_2_out, a, cary_in);
  or or_1 (cary_out, and_1_out, and_2_out, and_3_out);
  and and_3 (and_3_out, b, cary_in);
  ExactlyOne xor_1 (.out(s), .in0(a), .in1(b), .in2(cary_in));
endmodule

module my_2bit_full_adder (
  input  [1:0] a1a0,
  input  [1:0] b1b0,
  input  cary_in,
  output out_4,
  output [1:0] s1s0
);

  wire my_1bit_fadder_2_cary_out;

  my_1bit_fadder my_1bit_fadder_1 (
    .a(a1a0[1]), .b(b1b0[1]), .cary_in(my_1bit_fadder_2_cary_out), .cary_out(out_4), .s(s1s0[1]));
  my_1bit_fadder my_1bit_fadder_2 (
    .a(a1a0[0]), .b(b1b0[0]), .cary_in(cary_in), .cary_out(my_1bit_fadder_2_cary_out), .s(s1s0[0]));
endmodule

module my_4bit_adder (
  input  [3:0] a3a2a1a0,
  input  [3:0] b3b2b1b0,
  input  cary_in,
  output cary_out,
  output [3:0] s3s2s1s0
);

  wire my_2bit_full_adder_2_out_4;

  my_2bit_full_adder my_2bit_full_adder_1 (
    .a1a0(a3a2a1a0[3:2]), .b1b0(b3b2b1b0[3:2]), .cary_in(my_2bit_full_adder_2_out_4), .out_4(cary_out),
    .s1s0(s3s2s1s0[3:2]));
  my_2bit_full_adder my_2bit_full_adder_2 (
    .a1a0(a3a2a1a0[1:0]), .b1b0(b3b2b1b0[1:0]), .cary_in(cary_in), .out_4(my_2bit_full_adder_2_out_4),
    .s1s0(s3s2s1s0[1:0]));
endmodule

module my_8bit_fadder (
  input  cary_in,
  input  [7:0] a7a6a5a4a3a2a1,
  input  [7:0] b7b6b5b4b3b2b1,
  output cary_out,
  output [7:0] s7s6s5s4s3s2s1s0
);

  wire my_4bit_adder_2_cary_out;

  my_4bit_adder my_4bit_adder_1 (
    .a3a2a1a0(a7a6a5a4a3a2a1[7:4]), .b3b2b1b0(b7b6b5b4b3b2b1[7:4]), .cary_in(my_4bit_adder_2_cary_out),
    .cary_out(cary_out), .s3s2s1s0(s7s6s5s4s3s2s1s0[7:4]));
  my_4bit_adder my_4bit_adder_2 (
    .a3a2a1a0(a7a6a5a4a3a2a1[3:0]), .b3b2b1b0(b7b6b5b4b3b2b1[3:0]), .cary_in(cary_in),
    .cary_out(my_4bit_adder_2_cary_out), .s3s2s1s0(s7s6s5s4s3s2s1s0[3:0]));
endmodule

module my_16bit_fadder (
  input  [15:0] a15_a0,
  input  [15:0] b15_b0,
  input  cary_in,
  output cary_out,
  output [15:0] \output 
);

  wire my_8bit_fadder_2_cary_out;

  my_8bit_fadder my_8bit_fadder_1 (
    .a7a6a5a4a3a2a1(a15_a0[15:8]), .b7b6b5b4b3b2b1(b15_b0[15:8]), .cary_in(my_8bit_fadder_2_cary_out),
    .cary_out(cary_out), .s7s6s5s4s3s2s1s0(\output [15:8]));
  my_8bit_fadder my_8bit_fadder_2 (
    .a7a6a5a4a3a2a1(a15_a0[7:0]), .b7b6b5b4b3b2b1(b15_b0[7:0]), .cary_in(cary_in),
    .cary_out(my_8bit_fadder_2_cary_out), .s7s6s5s4s3s2s1s0(\output [7:0]));
endmodule

module my_6_to16_extender (
  input  [5:0] \input ,
  output [15:0] \output 
);


  assign \output  = {{11{\input [5]}}, \input [4:0]};
endmodule

module my_2_1_16bit_mux (
  input  [15:0] input1,
  input  [15:0] input2,
  input  selector,
  output [15:0] \output 
);

  wire [15:0] and_1_out, and_2_out, my_1_16_extender_1_output, not_1_out;

  assign not_1_out = ~my_1_16_extender_1_output;  // NOT_Gate not_1, 16 bits wide
  my_1_16_extender my_1_16_extender_1 (.\input (selector), .\output (my_1_16_extender_1_output));
  assign and_1_out = input1 & not_1_out;  // AND_Gate and_1, 16 bits wide
  assign and_2_out = input2 & my_1_16_extender_1_output;  // AND_Gate and_2, 16 bits wide
  assign \output  = and_1_out | and_2_out;  // OR_Gate or_1, 16 bits wide
endmodule

module my_9_to16bit_extender (
  input  [8:0] \input ,
  output [15:0] \output 
);


  assign \output  = {{7{1'b0}}, \input };
endmodule

module my_9_to_10_extender (
  input  [8:0] \input ,
  output [9:0] \output 
);


  assign \output  = {1'b0, \input };
endmodule

module my_2_1_10bit_mux (
  input  [9:0] input1,
  input  [9:0] input2,
  input  selector,
  output [9:0] \output 
);

  wire [9:0] and_1_out, and_2_out, my_1_to_10_extender_1_output, not_1_out;

  assign not_1_out = ~my_1_to_10_extender_1_output;  // NOT_Gate not_1, 10 bits wide
  my_1_to_10_extender my_1_to_10_extender_1 (.\input (selector), .\output (my_1_to_10_extender_1_output));
  assign and_1_out = input1 & not_1_out;  // AND_Gate and_1, 10 bits wide
  assign and_2_out = input2 & my_1_to_10_extender_1_output;  // AND_Gate and_2, 10 bits wide
  assign \output  = and_1_out | and_2_out;  // OR_Gate or_1, 10 bits wide
endmodule

module my_1_to_10_extender (
  input  \input ,
  output [9:0] \output 
);


  assign \output  = {10{\input }};
endmodule

module Program_Counter (
  input  if_0_add_1_else_jump,
  input  [15:0] jump_adress,
  input  enable,
  input  clk,
  output [15:0] \output 
);

  wire my_2_1_1bit_mux_1_output, my_2_1_1bit_mux_2_output, my_2_1_1bit_mux_3_output,
       my_2_1_1bit_mux_4_output, my_2_1_1bit_mux_5_output, my_2_1_1bit_mux_6_output,
       my_2_1_1bit_mux_7_output, my_2_1_1bit_mux_8_output, my_2_1_1bit_mux_9_output,
       my_2_1_1bit_mux_10_output, my_2_1_1bit_mux_11_output, my_2_1_1bit_mux_12_output,
       my_2_1_1bit_mux_13_output, my_2_1_1bit_mux_14_output, my_2_1_1bit_mux_15_output,
       my_2_1_1bit_mux_16_output, not_1_out;
  wire [15:0] my_2_1_16bit_mux_1_output, my_16bit_fadder_1_output;

  not not_1 (not_1_out, 1'b1);
  my_2_1_1bit_mux my_2_1_1bit_mux_1 (
    .input1(my_2_1_16bit_mux_1_output[1]), .input2(\output [1]), .selector(not_1_out),
    .\output (my_2_1_1bit_mux_1_output));
  my_2_1_1bit_mux my_2_1_1bit_mux_2 (
    .input1(my_2_1_16bit_mux_1_output[0]), .input2(\output [0]), .selector(not_1_out),
    .\output (my_2_1_1bit_mux_2_output));
  my_d_flipflop my_d_flipflop_1 (
    .\input (my_2_1_1bit_mux_2_output), .clk(clk), .\output (\output [0]), .enable(enable));
  my_d_flipflop my_d_flipflop_2 (
    .\input (my_2_1_1bit_mux_1_output), .clk(clk), .\output (\output [1]), .enable(enable));
  my_2_1_1bit_mux my_2_1_1bit_mux_3 (
    .input1(my_2_1_16bit_mux_1_output[2]), .input2(\output [2]), .selector(not_1_out),
    .\output (my_2_1_1bit_mux_3_output));
  my_d_flipflop my_d_flipflop_3 (
    .\input (my_2_1_1bit_mux_3_output), .clk(clk), .\output (\output [2]), .enable(enable));
  my_2_1_1bit_mux my_2_1_1bit_mux_4 (
    .input1(my_2_1_16bit_mux_1_output[3]), .input2(\output [3]), .selector(not_1_out),
    .\output (my_2_1_1bit_mux_4_output));
  my_d_flipflop my_d_flipflop_4 (
    .\input (my_2_1_1bit_mux_4_output), .clk(clk), .\output (\output [3]), .enable(enable));
  my_2_1_1bit_mux my_2_1_1bit_mux_5 (
    .input1(my_2_1_16bit_mux_1_output[4]), .input2(\output [4]), .selector(not_1_out),
    .\output (my_2_1_1bit_mux_5_output));
  my_d_flipflop my_d_flipflop_5 (
    .\input (my_2_1_1bit_mux_5_output), .clk(clk), .\output (\output [4]), .enable(enable));
  my_2_1_1bit_mux my_2_1_1bit_mux_6 (
    .input1(my_2_1_16bit_mux_1_output[5]), .input2(\output [5]), .selector(not_1_out),
    .\output (my_2_1_1bit_mux_6_output));
  my_d_flipflop my_d_flipflop_6 (
    .\input (my_2_1_1bit_mux_6_output), .clk(clk), .\output (\output [5]), .enable(enable));
  my_16bit_fadder my_16bit_fadder_1 (
    .a15_a0(16'h1), .b15_b0(\output ), .cary_in(1'b0), .\output (my_16bit_fadder_1_output));  // open: cary_out
  my_2_1_16bit_mux my_2_1_16bit_mux_1 (
    .input1(my_16bit_fadder_1_output), .input2(jump_adress), .selector(if_0_add_1_else_jump),
    .\output (my_2_1_16bit_mux_1_output));
  my_2_1_1bit_mux my_2_1_1bit_mux_7 (
    .input1(my_2_1_16bit_mux_1_output[6]), .input2(\output [6]), .selector(not_1_out),
    .\output (my_2_1_1bit_mux_7_output));
  my_d_flipflop my_d_flipflop_7 (
    .\input (my_2_1_1bit_mux_7_output), .clk(clk), .\output (\output [6]), .enable(enable));
  my_2_1_1bit_mux my_2_1_1bit_mux_8 (
    .input1(my_2_1_16bit_mux_1_output[7]), .input2(\output [7]), .selector(not_1_out),
    .\output (my_2_1_1bit_mux_8_output));
  my_d_flipflop my_d_flipflop_8 (
    .\input (my_2_1_1bit_mux_8_output), .clk(clk), .\output (\output [7]), .enable(enable));
  my_2_1_1bit_mux my_2_1_1bit_mux_9 (
    .input1(my_2_1_16bit_mux_1_output[8]), .input2(\output [8]), .selector(not_1_out),
    .\output (my_2_1_1bit_mux_9_output));
  my_d_flipflop my_d_flipflop_9 (
    .\input (my_2_1_1bit_mux_9_output), .clk(clk), .\output (\output [8]), .enable(enable));
  my_2_1_1bit_mux my_2_1_1bit_mux_10 (
    .input1(my_2_1_16bit_mux_1_output[10]), .input2(\output [10]), .selector(not_1_out),
    .\output (my_2_1_1bit_mux_10_output));
  my_2_1_1bit_mux my_2_1_1bit_mux_11 (
    .input1(my_2_1_16bit_mux_1_output[9]), .input2(\output [9]), .selector(not_1_out),
    .\output (my_2_1_1bit_mux_11_output));
  my_d_flipflop my_d_flipflop_10 (
    .\input (my_2_1_1bit_mux_11_output), .clk(clk), .\output (\output [9]), .enable(enable));
  my_d_flipflop my_d_flipflop_11 (
    .\input (my_2_1_1bit_mux_10_output), .clk(clk), .\output (\output [10]), .enable(enable));
  my_2_1_1bit_mux my_2_1_1bit_mux_12 (
    .input1(my_2_1_16bit_mux_1_output[11]), .input2(\output [11]), .selector(not_1_out),
    .\output (my_2_1_1bit_mux_12_output));
  my_d_flipflop my_d_flipflop_12 (
    .\input (my_2_1_1bit_mux_12_output), .clk(clk), .\output (\output [11]), .enable(enable));
  my_2_1_1bit_mux my_2_1_1bit_mux_13 (
    .input1(my_2_1_16bit_mux_1_output[12]), .input2(\output [12]), .selector(not_1_out),
    .\output (my_2_1_1bit_mux_13_output));
  my_d_flipflop my_d_flipflop_13 (
    .\input (my_2_1_1bit_mux_13_output), .clk(clk), .\output (\output [12]), .enable(enable));
  my_2_1_1bit_mux my_2_1_1bit_mux_14 (
    .input1(my_2_1_16bit_mux_1_output[13]), .input2(\output [13]), .selector(not_1_out),
    .\output (my_2_1_1bit_mux_14_output));
  my_d_flipflop my_d_flipflop_14 (
    .\input (my_2_1_1bit_mux_14_output), .clk(clk), .\output (\output [13]), .enable(enable));
  my_2_1_1bit_mux my_2_1_1bit_mux_15 (
    .input1(my_2_1_16bit_mux_1_output[14]), .input2(\output [14]), .selector(not_1_out),
    .\output (my_2_1_1bit_mux_15_output));
  my_d_flipflop my_d_flipflop_15 (
    .\input (my_2_1_1bit_mux_15_output), .clk(clk), .\output (\output [14]), .enable(enable));
  my_2_1_1bit_mux my_2_1_1bit_mux_16 (
    .input1(my_2_1_16bit_mux_1_output[15]), .input2(\output [15]), .selector(not_1_out),
    .\output (my_2_1_1bit_mux_16_output));
  my_d_flipflop my_d_flipflop_16 (
    .\input (my_2_1_1bit_mux_16_output), .clk(clk), .\output (\output [15]), .enable(enable));
endmodule

module my_16bit_eq_comparator (
  input  [15:0] input2,
  input  [15:0] input1,
  output \output 
);

  wire xnor_1_out, xnor_2_out, xnor_3_out, xnor_4_out, xnor_5_out, xnor_6_out, xnor_7_out, xnor_8_out,
       xnor_9_out, xnor_10_out, xnor_11_out, xnor_12_out, xnor_13_out, xnor_14_out, xnor_15_out, xnor_16_out;

  xnor xnor_1 (xnor_1_out, input1[15], input2[15]);
  xnor xnor_2 (xnor_2_out, input1[14], input2[14]);
  xnor xnor_3 (xnor_3_out, input1[13], input2[13]);
  xnor xnor_4 (xnor_4_out, input1[12], input2[12]);
  xnor xnor_5 (xnor_5_out, input1[11], input2[11]);
  xnor xnor_6 (xnor_6_out, input1[10], input2[10]);
  xnor xnor_7 (xnor_7_out, input1[8], input2[8]);
  xnor xnor_8 (xnor_8_out, input1[9], input2[9]);
  xnor xnor_9 (xnor_9_out, input1[7], input2[7]);
  and and_1 (\output , xnor_1_out, xnor_2_out, xnor_3_out, xnor_4_out, xnor_5_out, xnor_6_out, xnor_8_out, xnor_7_out, xnor_9_out, xnor_10_out, xnor_11_out, xnor_12_out, xnor_13_out, xnor_14_out, xnor_15_out, xnor_16_out);
  xnor xnor_10 (xnor_10_out, input1[6], input2[6]);
  xnor xnor_11 (xnor_11_out, input1[5], input2[5]);
  xnor xnor_12 (xnor_12_out, input1[4], input2[4]);
  xnor xnor_13 (xnor_13_out, input1[3], input2[3]);
  xnor xnor_14 (xnor_14_out, input1[2], input2[2]);
  xnor xnor_15 (xnor_15_out, input1[1], input2[1]);
  xnor xnor_16 (xnor_16_out, input1[0], input2[0]);
endmodule

module my_1bit_comparator (
  input  input1,
  input  input2,
  output \output 
);

  wire xnor_1_out, xnor_2_out;

  xnor xnor_1 (xnor_1_out, input1, input2);
  and and_1 (\output , xnor_1_out, xnor_2_out);
  xnor xnor_2 (xnor_2_out, input1, input2);
endmodule

module my_1bit_mag_comp (
  input  input1,
  input  input2,
  input  in_gt,
  input  in_eq,
  input  in_ls,
  output out_gt,
  output out_eq,
  output out_ls
);

  wire and_1_out, and_2_out, my_1bit_comparator_1_output, not_1_out, not_2_out, not_3_out, or_3_out;

  and and_1 (and_1_out, input1, in_eq, not_1_out);
  or or_1 (out_gt, in_gt, and_1_out);
  not not_1 (not_1_out, input2);
  my_1bit_comparator my_1bit_comparator_1 (.input1(input1), .input2(input2), .\output (my_1bit_comparator_1_output));
  not not_2 (not_2_out, input1);
  and and_2 (and_2_out, not_2_out, in_eq, input2);
  or or_2 (out_ls, in_ls, and_2_out);
  or or_3 (or_3_out, out_gt, out_ls);
  not not_3 (not_3_out, or_3_out);
  and and_3 (out_eq, my_1bit_comparator_1_output, not_3_out);
endmodule

module my_1bit_less_detector (
  input  input1,
  input  input2,
  input  in_3,
  output \output 
);

  wire and_1_out, not_1_out;

  not not_1 (not_1_out, input1);
  and and_1 (and_1_out, not_1_out, input2);
  or or_1 (\output , in_3, and_1_out);
endmodule

module my_16bit_mag_comparator (
  input  [15:0] input2,
  input  [15:0] input1,
  output gt,
  output eq,
  output ls
);

  wire my_1bit_mag_comp_1_out_eq, my_1bit_mag_comp_1_out_gt, my_1bit_mag_comp_1_out_ls,
       my_1bit_mag_comp_2_out_eq, my_1bit_mag_comp_2_out_gt, my_1bit_mag_comp_2_out_ls,
       my_1bit_mag_comp_3_out_eq, my_1bit_mag_comp_3_out_gt, my_1bit_mag_comp_3_out_ls,
       my_1bit_mag_comp_4_out_eq, my_1bit_mag_comp_4_out_gt, my_1bit_mag_comp_4_out_ls,
       my_1bit_mag_comp_5_out_eq, my_1bit_mag_comp_5_out_gt, my_1bit_mag_comp_5_out_ls,
       my_1bit_mag_comp_6_out_eq, my_1bit_mag_comp_6_out_gt, my_1bit_mag_comp_6_out_ls,
       my_1bit_mag_comp_7_out_eq, my_1bit_mag_comp_7_out_gt, my_1bit_mag_comp_7_out_ls,
       my_1bit_mag_comp_8_out_eq, my_1bit_mag_comp_8_out_gt, my_1bit_mag_comp_8_out_ls,
       my_1bit_mag_comp_9_out_eq, my_1bit_mag_comp_9_out_gt, my_1bit_mag_comp_9_out_ls,
       my_1bit_mag_comp_10_out_eq, my_1bit_mag_comp_10_out_gt, my_1bit_mag_comp_10_out_ls,
       my_1bit_mag_comp_11_out_eq, my_1bit_mag_comp_11_out_gt, my_1bit_mag_comp_11_out_ls,
       my_1bit_mag_comp_12_out_eq, my_1bit_mag_comp_12_out_gt, my_1bit_mag_comp_12_out_ls,
       my_1bit_mag_comp_13_out_eq, my_1bit_mag_comp_13_out_gt, my_1bit_mag_comp_13_out_ls,
       my_1bit_mag_comp_14_out_eq, my_1bit_mag_comp_14_out_gt, my_1bit_mag_comp_14_out_ls,
       my_1bit_mag_comp_16_out_eq, my_1bit_mag_comp_16_out_gt, my_1bit_mag_comp_16_out_ls;

  my_1bit_mag_comp my_1bit_mag_comp_1 (
    .in_gt(1'b0), .in_eq(1'b1), .in_ls(1'b0), .input1(input1[15]), .input2(input1[15]),
    .out_gt(my_1bit_mag_comp_1_out_gt), .out_eq(my_1bit_mag_comp_1_out_eq), .out_ls(my_1bit_mag_comp_1_out_ls));
  my_1bit_mag_comp my_1bit_mag_comp_2 (
    .in_gt(my_1bit_mag_comp_1_out_gt), .in_eq(my_1bit_mag_comp_1_out_eq), .in_ls(my_1bit_mag_comp_1_out_ls),
    .input1(input1[14]), .input2(input2[14]), .out_gt(my_1bit_mag_comp_2_out_gt),
    .out_eq(my_1bit_mag_comp_2_out_eq), .out_ls(my_1bit_mag_comp_2_out_ls));
  my_1bit_mag_comp my_1bit_mag_comp_3 (
    .in_gt(my_1bit_mag_comp_2_out_gt), .in_eq(my_1bit_mag_comp_2_out_eq), .in_ls(my_1bit_mag_comp_2_out_ls),
    .input1(input1[13]), .input2(input2[13]), .out_gt(my_1bit_mag_comp_3_out_gt),
    .out_eq(my_1bit_mag_comp_3_out_eq), .out_ls(my_1bit_mag_comp_3_out_ls));
  my_1bit_mag_comp my_1bit_mag_comp_4 (
    .in_gt(my_1bit_mag_comp_3_out_gt), .in_eq(my_1bit_mag_comp_3_out_eq), .in_ls(my_1bit_mag_comp_3_out_ls),
    .input1(input1[12]), .input2(input2[12]), .out_gt(my_1bit_mag_comp_4_out_gt),
    .out_eq(my_1bit_mag_comp_4_out_eq), .out_ls(my_1bit_mag_comp_4_out_ls));
  my_1bit_mag_comp my_1bit_mag_comp_5 (
    .in_gt(my_1bit_mag_comp_4_out_gt), .in_eq(my_1bit_mag_comp_4_out_eq), .in_ls(my_1bit_mag_comp_4_out_ls),
    .input1(input1[11]), .input2(input2[11]), .out_gt(my_1bit_mag_comp_5_out_gt),
    .out_eq(my_1bit_mag_comp_5_out_eq), .out_ls(my_1bit_mag_comp_5_out_ls));
  my_1bit_mag_comp my_1bit_mag_comp_6 (
    .in_gt(my_1bit_mag_comp_5_out_gt), .in_eq(my_1bit_mag_comp_5_out_eq), .in_ls(my_1bit_mag_comp_5_out_ls),
    .input1(input1[10]), .input2(input2[10]), .out_gt(my_1bit_mag_comp_6_out_gt),
    .out_eq(my_1bit_mag_comp_6_out_eq), .out_ls(my_1bit_mag_comp_6_out_ls));
  my_1bit_mag_comp my_1bit_mag_comp_7 (
    .in_gt(my_1bit_mag_comp_6_out_gt), .in_eq(my_1bit_mag_comp_6_out_eq), .in_ls(my_1bit_mag_comp_6_out_ls),
    .input1(input1[9]), .input2(input2[9]), .out_gt(my_1bit_mag_comp_7_out_gt),
    .out_eq(my_1bit_mag_comp_7_out_eq), .out_ls(my_1bit_mag_comp_7_out_ls));
  my_1bit_mag_comp my_1bit_mag_comp_8 (
    .in_gt(my_1bit_mag_comp_7_out_gt), .in_eq(my_1bit_mag_comp_7_out_eq), .in_ls(my_1bit_mag_comp_7_out_ls),
    .input1(input1[8]), .input2(input2[8]), .out_gt(my_1bit_mag_comp_8_out_gt),
    .out_eq(my_1bit_mag_comp_8_out_eq), .out_ls(my_1bit_mag_comp_8_out_ls));
  my_1bit_mag_comp my_1bit_mag_comp_9 (
    .in_gt(my_1bit_mag_comp_8_out_gt), .in_eq(my_1bit_mag_comp_8_out_eq), .in_ls(my_1bit_mag_comp_8_out_ls),
    .input1(input1[7]), .input2(input2[7]), .out_gt(my_1bit_mag_comp_9_out_gt),
    .out_eq(my_1bit_mag_comp_9_out_eq), .out_ls(my_1bit_mag_comp_9_out_ls));
  my_1bit_mag_comp my_1bit_mag_comp_10 (
    .in_gt(my_1bit_mag_comp_9_out_gt), .in_eq(my_1bit_mag_comp_9_out_eq), .in_ls(my_1bit_mag_comp_9_out_ls),
    .input1(input1[6]), .input2(input2[6]), .out_gt(my_1bit_mag_comp_10_out_gt),
    .out_eq(my_1bit_mag_comp_10_out_eq), .out_ls(my_1bit_mag_comp_10_out_ls));
  my_1bit_mag_comp my_1bit_mag_comp_11 (
    .in_gt(my_1bit_mag_comp_10_out_gt), .in_eq(my_1bit_mag_comp_10_out_eq),
    .in_ls(my_1bit_mag_comp_10_out_ls), .input1(input1[5]), .input2(input2[5]),
    .out_gt(my_1bit_mag_comp_11_out_gt), .out_eq(my_1bit_mag_comp_11_out_eq),
    .out_ls(my_1bit_mag_comp_11_out_ls));
  my_1bit_mag_comp my_1bit_mag_comp_12 (
    .in_gt(my_1bit_mag_comp_11_out_gt), .in_eq(my_1bit_mag_comp_11_out_eq),
    .in_ls(my_1bit_mag_comp_11_out_ls), .input1(input1[4]), .input2(input2[4]),
    .out_gt(my_1bit_mag_comp_12_out_gt), .out_eq(my_1bit_mag_comp_12_out_eq),
    .out_ls(my_1bit_mag_comp_12_out_ls));
  my_1bit_mag_comp my_1bit_mag_comp_13 (
    .in_gt(my_1bit_mag_comp_12_out_gt), .in_eq(my_1bit_mag_comp_12_out_eq),
    .in_ls(my_1bit_mag_comp_12_out_ls), .input1(input1[3]), .input2(input2[3]),
    .out_gt(my_1bit_mag_comp_13_out_gt), .out_eq(my_1bit_mag_comp_13_out_eq),
    .out_ls(my_1bit_mag_comp_13_out_ls));
  my_1bit_mag_comp my_1bit_mag_comp_14 (
    .in_gt(my_1bit_mag_comp_13_out_gt), .in_eq(my_1bit_mag_comp_13_out_eq),
    .in_ls(my_1bit_mag_comp_13_out_ls), .input1(input1[2]), .input2(input2[2]),
    .out_gt(my_1bit_mag_comp_14_out_gt), .out_eq(my_1bit_mag_comp_14_out_eq),
    .out_ls(my_1bit_mag_comp_14_out_ls));
  my_1bit_mag_comp my_1bit_mag_comp_15 (
    .in_gt(my_1bit_mag_comp_16_out_gt), .in_eq(my_1bit_mag_comp_16_out_eq),
    .in_ls(my_1bit_mag_comp_16_out_ls), .input1(input1[0]), .input2(input2[0]), .out_gt(gt), .out_eq(eq),
    .out_ls(ls));
  my_1bit_mag_comp my_1bit_mag_comp_16 (
    .in_gt(my_1bit_mag_comp_14_out_gt), .in_eq(my_1bit_mag_comp_14_out_eq),
    .in_ls(my_1bit_mag_comp_14_out_ls), .input1(input1[1]), .input2(input2[1]),
    .out_gt(my_1bit_mag_comp_16_out_gt), .out_eq(my_1bit_mag_comp_16_out_eq),
    .out_ls(my_1bit_mag_comp_16_out_ls));

  assign input2[15] = input1[15];
endmodule
